// Logisim project projet.circ as structural Verilog
module main (
  input  reset_debug,
  output [4:0] out_2,
  output led_9,
  output led_8,
  output led_7,
  output led_6,
  output led_5,
  output led_4,
  output led_3,
  output led_2,
  output led_1,
  output led_0,
  output buzzer_0,
  output buzzer_1
);

  wire B_0_out, B_1_out, clock_1_out, clock_2_out, clock_3_out, clock_4_out, debouncer_1_out_2,
       debouncer_2_out_2, dipswitch_1_sw1, dipswitch_1_sw2, dipswitch_1_sw3, dipswitch_1_sw4,
       dipswitch_1_sw5, dipswitch_1_sw6, dipswitch_1_sw7, dipswitch_1_sw8, dipswitch_1_sw9, dipswitch_1_sw10,
       Fa_out, FaD5_out, La6_out, Mi_out, output_logic_1_a, output_logic_1_a_2, output_logic_1_b,
       output_logic_1_b_2, output_logic_1_c, output_logic_1_c_2, output_logic_1_d, output_logic_1_d_2,
       output_logic_1_e, output_logic_1_e_2, output_logic_1_f, output_logic_1_f_2, output_logic_1_g,
       output_logic_1_g_2, output_logic_1_p, output_logic_1_p_2, output_logic_2_a, output_logic_2_b,
       output_logic_2_c, output_logic_2_d, output_logic_2_e, output_logic_2_f, output_logic_2_g,
       output_logic_2_p, output_logic_3_a, output_logic_3_b, output_logic_3_c, output_logic_3_d,
       output_logic_3_e, output_logic_3_f, output_logic_3_g, output_logic_3_p, output_logic_4_a,
       output_logic_4_b, output_logic_4_c, output_logic_4_d, output_logic_4_e, output_logic_4_f,
       output_logic_4_g, output_logic_4_p, output_logic_5_a, output_logic_5_b, output_logic_5_c,
       output_logic_5_d, output_logic_5_e, output_logic_5_f, output_logic_5_g, output_logic_5_p, ReD5_out,
       reset_out, Si5_out, Si6_out, Sol5_out, transition_logic_1_s_0, transition_logic_1_s_1,
       transition_logic_1_s_2, transition_logic_1_s_3;
  wire [3:0] d_ff_4_q;
  wire [4:0] multiplexer_4_out, multiplexer_5_out, multiplexer_6_out, multiplexer_7_out, multiplexer_8_out,
       multiplexer_9_out, set_time_setter_1_o_0, set_time_setter_1_o_1, set_time_setter_1_o_2,
       set_time_setter_1_o_3, set_time_setter_1_o_4, set_time_setter_1_o_5, time_to_binary_converter_1_o_0,
       time_to_binary_converter_1_o_1, time_to_binary_converter_2_o_0, time_to_binary_converter_2_o_1,
       time_to_binary_converter_3_o_1;
  wire [5:0] binary_to_time_converter_1_out_3, binary_to_time_converter_2_out_3,
       binary_to_time_converter_3_out_3, memory_alarm_1_hour, memory_alarm_1_min, memory_alarm_1_seconds,
       memory_time_1_h_out, memory_time_1_m_out, memory_time_1_s_out, multiplexer_1_out, multiplexer_2_out,
       multiplexer_3_out;
  wire [11:0] demultiplexer_1_out3, transition_logic_1_input_bus;

  Button B_1 (.out(B_1_out));
  Button B_0 (.out(B_0_out));
  debouncer debouncer_1 (.I_0(B_1_out), .out_2(debouncer_1_out_2));
  debouncer debouncer_2 (.I_0(B_0_out), .out_2(debouncer_2_out_2));
  DipSwitch #(.number(10)) dipswitch_1 (
    .sw1(dipswitch_1_sw1), .sw2(dipswitch_1_sw2), .sw3(dipswitch_1_sw3), .sw4(dipswitch_1_sw4),
    .sw5(dipswitch_1_sw5), .sw6(dipswitch_1_sw6), .sw7(dipswitch_1_sw7), .sw8(dipswitch_1_sw8),
    .sw9(dipswitch_1_sw9), .sw10(dipswitch_1_sw10));
  Clock #(.highDuration(61162), .lowDuration(61162)) Do1 ();  // open: out
  Clock #(.highDuration(57720), .lowDuration(57720)) DoD1 ();  // open: out
  Clock #(.highDuration(54481), .lowDuration(54481)) Re1 ();  // open: out
  Clock #(.highDuration(51427), .lowDuration(51427)) ReD1 ();  // open: out
  Clock #(.highDuration(48544), .lowDuration(48544)) Mi1 ();  // open: out
  Clock #(.highDuration(45819), .lowDuration(45819)) Fa1 ();  // open: out
  Clock #(.highDuration(43243), .lowDuration(43243)) FaD1 ();  // open: out
  Clock #(.highDuration(40816), .lowDuration(40816)) Sol1 ();  // open: out
  Clock #(.highDuration(38528), .lowDuration(38528)) SolD1 ();  // open: out
  Clock #(.highDuration(36364), .lowDuration(36364)) La1 ();  // open: out
  Clock #(.highDuration(34323), .lowDuration(268)) SiB1 ();  // open: out
  Clock #(.highDuration(32394), .lowDuration(32394)) Si1 ();  // open: out
  Clock #(.highDuration(30576), .lowDuration(30576)) Do2 ();  // open: out
  Clock #(.highDuration(28860), .lowDuration(28860)) DoD2 ();  // open: out
  Clock #(.highDuration(27241), .lowDuration(27241)) Re2 ();  // open: out
  Clock #(.highDuration(25714), .lowDuration(25714)) ReD2 ();  // open: out
  Clock #(.highDuration(24269), .lowDuration(24269)) Mi2 ();  // open: out
  Clock #(.highDuration(22907), .lowDuration(284)) Fa2 ();  // open: out
  Clock #(.highDuration(21622), .lowDuration(21622)) FaD2 ();  // open: out
  Clock #(.highDuration(20408), .lowDuration(20408)) Sol2 ();  // open: out
  Clock #(.highDuration(19262), .lowDuration(19262)) SolD2 ();  // open: out
  Clock #(.highDuration(18182), .lowDuration(18182)) La2 ();  // open: out
  Clock #(.highDuration(17161), .lowDuration(17161)) SiB2 ();  // open: out
  Clock #(.highDuration(16198), .lowDuration(16198)) Si2 ();  // open: out
  Clock #(.highDuration(15289), .lowDuration(15289)) Do3 ();  // open: out
  Clock #(.highDuration(14431), .lowDuration(14431)) DoD3 ();  // open: out
  Clock #(.highDuration(13621), .lowDuration(13621)) Re3 ();  // open: out
  Clock #(.highDuration(12857), .lowDuration(12857)) ReD3 ();  // open: out
  Clock #(.highDuration(12135)) Mi3 ();  // open: out
  Clock #(.highDuration(11454), .lowDuration(11454)) Fa3 ();  // open: out
  Clock #(.highDuration(10811), .lowDuration(268)) FaD3 ();  // open: out
  Clock #(.highDuration(10204), .lowDuration(10204)) Sol3 ();  // open: out
  Clock #(.highDuration(9632), .lowDuration(9632)) SolD3 ();  // open: out
  Clock #(.highDuration(9091), .lowDuration(9091)) La3 ();  // open: out
  Clock #(.highDuration(8581), .lowDuration(8581)) SiB3 ();  // open: out
  Clock #(.highDuration(8099), .lowDuration(8099)) Si3 ();  // open: out
  Clock #(.highDuration(7644), .lowDuration(7644)) Do4 ();  // open: out
  Clock #(.highDuration(7216), .lowDuration(7216)) DoD4 ();  // open: out
  Clock #(.highDuration(6811), .lowDuration(6811)) Re4 ();  // open: out
  Clock #(.highDuration(6428), .lowDuration(6428)) ReD4 ();  // open: out
  Clock #(.highDuration(6067), .lowDuration(6067)) Mi4 ();  // open: out
  Clock #(.highDuration(5727), .lowDuration(284)) Fa4 ();  // open: out
  Clock #(.highDuration(5406), .lowDuration(5406)) FaD4 ();  // open: out
  Clock #(.highDuration(5102), .lowDuration(253)) Sol4 ();  // open: out
  Clock #(.highDuration(4816)) SolD4 ();  // open: out
  Clock #(.highDuration(4545), .lowDuration(4545)) La4 ();  // open: out
  Clock #(.highDuration(4290), .lowDuration(4290)) SiB4 ();  // open: out
  Clock #(.highDuration(4050), .lowDuration(4050)) Si4 ();  // open: out
  Clock #(.highDuration(3822), .lowDuration(3822)) Do5 ();  // open: out
  Clock #(.highDuration(3608), .lowDuration(3608)) DoD5 ();  // open: out
  Clock #(.highDuration(3405), .lowDuration(3405)) Re5 ();  // open: out
  Clock #(.highDuration(3214), .lowDuration(3214)) ReD5 (.out(ReD5_out));
  Clock #(.highDuration(3034), .lowDuration(3034)) Mi (.out(Mi_out));
  Clock #(.highDuration(2863), .lowDuration(2863)) Fa (.out(Fa_out));
  Clock #(.highDuration(2703), .lowDuration(2703)) FaD5 (.out(FaD5_out));
  Clock #(.highDuration(2551), .lowDuration(2551)) Sol5 (.out(Sol5_out));
  Clock #(.highDuration(2408), .lowDuration(2408)) SolD5 ();  // open: out
  Clock #(.highDuration(2273), .lowDuration(2273)) La5 ();  // open: out
  Clock #(.highDuration(2145), .lowDuration(2145)) SiB5 ();  // open: out
  Clock #(.highDuration(2025), .lowDuration(2025)) Si5 (.out(Si5_out));
  Clock #(.highDuration(1911), .lowDuration(1911)) Do6 ();  // open: out
  Clock #(.highDuration(1804), .lowDuration(1804)) DoD6 ();  // open: out
  Clock #(.highDuration(1703), .lowDuration(1703)) Re6 ();  // open: out
  Clock #(.highDuration(1607), .lowDuration(1607)) ReD6 ();  // open: out
  Clock #(.highDuration(1517), .lowDuration(1517)) Mi6 ();  // open: out
  Clock #(.highDuration(1432), .lowDuration(1432)) Fa6 ();  // open: out
  Clock #(.highDuration(1351), .lowDuration(1351)) FaD6 ();  // open: out
  Clock #(.highDuration(1276), .lowDuration(1276)) Sol6 ();  // open: out
  Clock #(.highDuration(1204), .lowDuration(1204)) SolD6 ();  // open: out
  Clock #(.highDuration(1136), .lowDuration(1136)) La6 (.out(La6_out));
  Clock #(.highDuration(1073), .lowDuration(1073)) Sib6 ();  // open: out
  Clock #(.highDuration(1012), .lowDuration(1012)) Si6 (.out(Si6_out));
  Clock #(.highDuration(956), .lowDuration(956)) Do7 ();  // open: out
  Clock #(.highDuration(902), .lowDuration(902)) DoD7 ();  // open: out
  Clock #(.highDuration(851), .lowDuration(851)) Re7 ();  // open: out
  Clock #(.highDuration(804), .lowDuration(804)) ReD7 ();  // open: out
  Clock #(.highDuration(758), .lowDuration(758)) Mi7 ();  // open: out
  Clock #(.highDuration(716), .lowDuration(716)) Fa7 ();  // open: out
  Clock #(.highDuration(676), .lowDuration(676)) FaD7 ();  // open: out
  Clock #(.highDuration(638), .lowDuration(638)) Sol7 ();  // open: out
  Clock #(.highDuration(602), .lowDuration(602)) SolD7 ();  // open: out
  Clock #(.highDuration(568), .lowDuration(568)) La7 ();  // open: out
  Clock #(.highDuration(536), .lowDuration(536)) SiB7 ();  // open: out
  Clock #(.highDuration(506), .lowDuration(506)) Si7 ();  // open: out
  Clock #(.highDuration(478), .lowDuration(478)) Do8 ();  // open: out
  Clock #(.highDuration(451), .lowDuration(451)) DoD8 ();  // open: out
  Clock #(.highDuration(426), .lowDuration(426)) Re8 ();  // open: out
  Clock #(.highDuration(402), .lowDuration(402)) ReD8 ();  // open: out
  Clock #(.highDuration(379), .lowDuration(379)) Mi8 ();  // open: out
  Clock #(.highDuration(358), .lowDuration(358)) Fa8 ();  // open: out
  Clock #(.highDuration(338), .lowDuration(338)) FaD8 ();  // open: out
  Clock #(.highDuration(319), .lowDuration(319)) Sol8 ();  // open: out
  Clock #(.highDuration(301), .lowDuration(301)) SolD8 ();  // open: out
  Clock #(.highDuration(284), .lowDuration(284)) La8 ();  // open: out
  Clock #(.highDuration(268), .lowDuration(268)) SiB8 ();  // open: out
  Clock #(.highDuration(253), .lowDuration(253)) Si8 ();  // open: out
  reset_mode reset_mode_1 (.B_1(debouncer_1_out_2), .B_0(debouncer_2_out_2));  // open: R
  transition_logic transition_logic_1 (
    .C_3(d_ff_4_q[3]), .C_2(d_ff_4_q[2]), .C_1(d_ff_4_q[1]), .C_0(d_ff_4_q[0]), .B_1(debouncer_1_out_2),
    .B_0(debouncer_2_out_2), .DS_9(dipswitch_1_sw10), .DS_8(dipswitch_1_sw9), .DS_7(dipswitch_1_sw8),
    .DS_6(dipswitch_1_sw7), .DS_5(dipswitch_1_sw6), .DS_4(dipswitch_1_sw5), .DS_3(dipswitch_1_sw4),
    .DS_2(dipswitch_1_sw3), .DS_1(dipswitch_1_sw2), .DS_0(dipswitch_1_sw1), .S_3(transition_logic_1_s_3),
    .S_2(transition_logic_1_s_2), .S_1(transition_logic_1_s_1), .S_0(transition_logic_1_s_0),
    .input_bus(transition_logic_1_input_bus));
  Button reset (.out(reset_out));
  Clock clock_1 (.out(clock_1_out));
  D_Flip_Flop d_ff_1 (
    .D(transition_logic_1_s_3), .clk(clock_1_out), .Q(d_ff_4_q[3]), .reset(reset_debug));  // open: Qn, preset
  D_Flip_Flop d_ff_2 (
    .D(transition_logic_1_s_2), .clk(clock_1_out), .Q(d_ff_4_q[2]), .reset(reset_debug));  // open: Qn, preset
  D_Flip_Flop d_ff_3 (
    .D(transition_logic_1_s_1), .clk(clock_1_out), .Q(d_ff_4_q[1]), .reset(reset_debug));  // open: Qn, preset
  D_Flip_Flop d_ff_4 (
    .D(transition_logic_1_s_0), .clk(clock_1_out), .Q(d_ff_4_q[0]), .reset(reset_debug));  // open: Qn, preset
  Clock #(.highDuration(400000), .lowDuration(400000)) clock_2 (.out(clock_2_out));
  Clock clock_3 (.out(clock_3_out));
  music_givenTheme music_givenTheme_1 (
    .Ds(ReD5_out), .E(Mi_out), .F(Fa_out), .Fs(FaD5_out), .G(Sol5_out), .B(Si5_out), .A2(La6_out),
    .B2(Si6_out), .reset(reset_out), .music_clock(clock_2_out), .in_11(clock_3_out), .freq(buzzer_1));
  Demultiplexer #(.select(4), .width(12), .enable("false")) demultiplexer_1 (
    .out3(demultiplexer_1_out3), .in(transition_logic_1_input_bus), .sel(d_ff_4_q));  // open: out0, out1, out2, out4, out5, out6, out7, out8, out9, out10, out11, out12, out13, out14, out15
  Clock clock_4 (.out(clock_4_out));
  binary_to_time_converter binary_to_time_converter_1 (
    .in_1(set_time_setter_1_o_5), .in_2(set_time_setter_1_o_4), .out_3(binary_to_time_converter_1_out_3));
  binary_to_time_converter binary_to_time_converter_2 (
    .in_1(set_time_setter_1_o_3), .in_2(set_time_setter_1_o_2), .out_3(binary_to_time_converter_2_out_3));
  binary_to_time_converter binary_to_time_converter_3 (
    .in_1(set_time_setter_1_o_1), .in_2(set_time_setter_1_o_0), .out_3(binary_to_time_converter_3_out_3));
  memory_alarm memory_alarm_1 (
    .reset(reset_debug), .hour(memory_alarm_1_hour), .min(memory_alarm_1_min),
    .seconds(memory_alarm_1_seconds));  // open: hour_in, min_in, sec_in, set, enable
  memory_time memory_time_1 (
    .set_hour(binary_to_time_converter_1_out_3), .set_min(binary_to_time_converter_2_out_3),
    .set_sec(binary_to_time_converter_3_out_3), .clock(clock_4_out), .reset(reset_debug),
    .h_out(memory_time_1_h_out), .m_out(memory_time_1_m_out), .s_out(memory_time_1_s_out));  // open: load, carry
  set_time_setter set_time_setter_1 (
    .I_5(time_to_binary_converter_1_o_1), .I_4(time_to_binary_converter_1_o_0),
    .I_3(time_to_binary_converter_2_o_1), .I_2(time_to_binary_converter_2_o_0),
    .I_1(time_to_binary_converter_3_o_1), .I_0(out_2), .input_bus(demultiplexer_1_out3), .mode_on(d_ff_4_q),
    .R(reset_debug), .O_5(set_time_setter_1_o_5), .O_4(set_time_setter_1_o_4), .O_3(set_time_setter_1_o_3),
    .O_2(set_time_setter_1_o_2), .O_1(set_time_setter_1_o_1), .O_0(set_time_setter_1_o_0));
  Multiplexer #(.select(3), .width(6), .enable("false")) multiplexer_1 (
    .in6(memory_alarm_1_hour), .in7(memory_time_1_h_out), .out(multiplexer_1_out), .sel(3'b111));  // open: in0, in1, in2, in3, in4, in5
  Multiplexer #(.select(3), .width(6), .enable("false")) multiplexer_2 (
    .in6(memory_alarm_1_min), .in7(memory_time_1_m_out), .out(multiplexer_2_out), .sel(3'b111));  // open: in0, in1, in2, in3, in4, in5
  Multiplexer #(.select(3), .width(6), .enable("false")) multiplexer_3 (
    .in6(memory_alarm_1_seconds), .in7(memory_time_1_s_out), .out(multiplexer_3_out), .sel(3'b111));  // open: in0, in1, in2, in3, in4, in5
  time_to_binary_converter time_to_binary_converter_1 (
    .t_in(multiplexer_1_out), .O_1(time_to_binary_converter_1_o_1), .O_0(time_to_binary_converter_1_o_0));
  time_to_binary_converter time_to_binary_converter_2 (
    .t_in(multiplexer_2_out), .O_1(time_to_binary_converter_2_o_1), .O_0(time_to_binary_converter_2_o_0));
  time_to_binary_converter time_to_binary_converter_3 (
    .t_in(multiplexer_3_out), .O_1(time_to_binary_converter_3_o_1), .O_0(out_2));
  Multiplexer #(.select(4), .width(5), .enable("false")) multiplexer_4 (
    .in0(time_to_binary_converter_1_o_1), .in3(set_time_setter_1_o_5), .out(multiplexer_4_out), .sel(d_ff_4_q));  // open: in1, in2, in4, in5, in6, in7, in8, in9, in10, in11, in12, in13, in14, in15
  Multiplexer #(.select(4), .width(5), .enable("false")) multiplexer_5 (
    .in0(time_to_binary_converter_1_o_0), .in3(set_time_setter_1_o_4), .out(multiplexer_5_out), .sel(d_ff_4_q));  // open: in1, in2, in4, in5, in6, in7, in8, in9, in10, in11, in12, in13, in14, in15
  Multiplexer #(.select(4), .width(5), .enable("false")) multiplexer_6 (
    .in0(time_to_binary_converter_2_o_1), .in3(set_time_setter_1_o_3), .out(multiplexer_6_out), .sel(d_ff_4_q));  // open: in1, in2, in4, in5, in6, in7, in8, in9, in10, in11, in12, in13, in14, in15
  Multiplexer #(.select(4), .width(5), .enable("false")) multiplexer_7 (
    .in0(time_to_binary_converter_2_o_0), .in3(set_time_setter_1_o_2), .out(multiplexer_7_out), .sel(d_ff_4_q));  // open: in1, in2, in4, in5, in6, in7, in8, in9, in10, in11, in12, in13, in14, in15
  Multiplexer #(.select(4), .width(5), .enable("false")) multiplexer_8 (
    .in0(time_to_binary_converter_3_o_1), .in3(set_time_setter_1_o_1), .out(multiplexer_8_out), .sel(d_ff_4_q));  // open: in1, in2, in4, in5, in6, in7, in8, in9, in10, in11, in12, in13, in14, in15
  Multiplexer #(.select(4), .width(5), .enable("false")) multiplexer_9 (
    .in0(out_2), .in3(set_time_setter_1_o_0), .out(multiplexer_9_out), .sel(d_ff_4_q));  // open: in1, in2, in4, in5, in6, in7, in8, in9, in10, in11, in12, in13, in14, in15
  output_logic output_logic_1 (
    .i(multiplexer_4_out), .a(output_logic_1_a), .b(output_logic_1_b), .c(output_logic_1_c_2),
    .d(output_logic_1_d), .e(output_logic_1_e), .f(output_logic_1_f), .g(output_logic_1_g_2),
    .p(output_logic_1_p));  // open: point
  output_logic output_logic_1_dup2 (
    .i(multiplexer_5_out), .a(output_logic_1_a_2), .b(output_logic_1_b_2), .c(output_logic_1_c),
    .d(output_logic_1_d_2), .e(output_logic_1_e_2), .f(output_logic_1_f_2), .g(output_logic_1_g),
    .p(output_logic_1_p_2));  // open: point
  output_logic output_logic_2 (
    .i(multiplexer_6_out), .a(output_logic_2_a), .b(output_logic_2_b), .c(output_logic_2_c),
    .d(output_logic_2_d), .e(output_logic_2_e), .f(output_logic_2_f), .g(output_logic_2_g),
    .p(output_logic_2_p));  // open: point
  output_logic output_logic_3 (
    .i(multiplexer_7_out), .a(output_logic_3_a), .b(output_logic_3_b), .c(output_logic_3_c),
    .d(output_logic_3_d), .e(output_logic_3_e), .f(output_logic_3_f), .g(output_logic_3_g),
    .p(output_logic_3_p));  // open: point
  output_logic output_logic_4 (
    .i(multiplexer_8_out), .a(output_logic_4_a), .b(output_logic_4_b), .c(output_logic_4_c),
    .d(output_logic_4_d), .e(output_logic_4_e), .f(output_logic_4_f), .g(output_logic_4_g),
    .p(output_logic_4_p));  // open: point
  output_logic output_logic_5 (
    .i(multiplexer_9_out), .a(output_logic_5_a), .b(output_logic_5_b), .c(output_logic_5_c),
    .d(output_logic_5_d), .e(output_logic_5_e), .f(output_logic_5_f), .g(output_logic_5_g),
    .p(output_logic_5_p));  // open: point
  _7_Segment_Display L_7_Segment_Display_1 (
    .g(output_logic_1_g_2), .f(output_logic_1_f), .a(output_logic_1_a), .b(output_logic_1_b),
    .e(output_logic_1_e), .d(output_logic_1_d), .c(output_logic_1_c_2), .dp(output_logic_1_p));
  _7_Segment_Display u_7_segment_display_1 (
    .g(output_logic_1_g), .f(output_logic_1_f_2), .a(output_logic_1_a_2), .b(output_logic_1_b_2),
    .e(output_logic_1_e_2), .d(output_logic_1_d_2), .c(output_logic_1_c), .dp(output_logic_1_p_2));
  _7_Segment_Display u_7_segment_display_2 (
    .g(output_logic_2_g), .f(output_logic_2_f), .a(output_logic_2_a), .b(output_logic_2_b),
    .e(output_logic_2_e), .d(output_logic_2_d), .c(output_logic_2_c), .dp(output_logic_2_p));
  _7_Segment_Display u_7_segment_display_3 (
    .g(output_logic_3_g), .f(output_logic_3_f), .a(output_logic_3_a), .b(output_logic_3_b),
    .e(output_logic_3_e), .d(output_logic_3_d), .c(output_logic_3_c), .dp(output_logic_3_p));
  _7_Segment_Display u_7_segment_display_4 (
    .g(output_logic_4_g), .f(output_logic_4_f), .a(output_logic_4_a), .b(output_logic_4_b),
    .e(output_logic_4_e), .d(output_logic_4_d), .c(output_logic_4_c), .dp(output_logic_4_p));
  _7_Segment_Display u_7_segment_display_5 (
    .g(output_logic_5_g), .f(output_logic_5_f), .a(output_logic_5_a), .b(output_logic_5_b),
    .e(output_logic_5_e), .d(output_logic_5_d), .c(output_logic_5_c), .dp(output_logic_5_p));

  assign buzzer_0 = 1'b0;
  assign led_0 = 1'b0;
  assign led_1 = 1'b0;
  assign led_2 = 1'b0;
  assign led_3 = 1'b0;
  assign led_4 = 1'b0;
  assign led_5 = 1'b0;
  assign led_6 = 1'b0;
  assign led_7 = 1'b0;
  assign led_8 = 1'b0;
  assign led_9 = 1'b0;
endmodule

module output_logic (
  input  point,
  input  [4:0] i,
  output a,
  output b,
  output c,
  output d,
  output e,
  output f,
  output g,
  output p
);

  wire nand_1_out, nand_2_out, nand_3_out, nand_4_out, nand_5_out, nand_6_out, nand_7_out, nand_8_out,
       nand_9_out, nand_10_out, nand_11_out, nand_12_out, nand_13_out, nand_14_out, nand_15_out, nand_16_out,
       nand_17_out, nand_18_out, nand_19_out, nand_20_out, nand_21_out, nand_22_out, nand_23_out,
       nand_24_out, nand_25_out, nand_26_out, nand_27_out, nand_28_out, nand_29_out, nand_30_out,
       nand_31_out, nand_32_out, nand_33_out, nand_34_out, nand_35_out, nand_36_out, nand_37_out,
       nand_38_out, nand_39_out, nand_40_out, nand_41_out, nand_42_out, nand_43_out, nand_44_out,
       nand_45_out, nand_46_out, nand_47_out, nand_48_out, nand_49_out, nand_50_out, nand_51_out,
       nand_52_out, nand_53_out, nand_54_out, nand_55_out, nand_56_out, nand_57_out, nand_58_out,
       nand_59_out, nand_60_out, nand_61_out, nand_62_out, nand_63_out, nand_64_out, nand_65_out,
       nand_66_out, nand_67_out, nand_68_out, nand_69_out, nand_70_out, nand_71_out, nand_72_out,
       nand_73_out, nand_74_out, nand_75_out, nand_76_out, nand_77_out, nand_78_out, nand_79_out,
       nand_80_out, nand_81_out, nand_82_out, nand_83_out, nand_84_out, nand_85_out, nand_86_out,
       nand_87_out, nand_88_out, nand_89_out, nand_90_out, nand_91_out, nand_92_out, nand_93_out,
       nand_94_out, nand_95_out, nand_96_out, nand_97_out, nand_98_out, nand_99_out, nand_100_out,
       nand_101_out, nand_102_out, nand_103_out, nand_104_out, nand_105_out, nand_106_out, nand_107_out,
       nand_108_out, nand_109_out, nand_110_out, nand_111_out, nand_112_out, nand_113_out, nand_114_out,
       nand_115_out, nand_116_out, nand_117_out, nand_118_out, nand_119_out, nand_120_out, nand_121_out,
       nand_122_out, nand_123_out, nand_124_out, nand_125_out, nand_126_out, nand_127_out, nand_128_out,
       nand_129_out, nand_130_out, nand_131_out, nand_132_out, nand_133_out, nand_134_out, nand_135_out,
       nand_136_out, nand_137_out, nand_138_out, nand_139_out, nand_140_out, nand_141_out, nand_142_out,
       nand_143_out, nand_144_out, nand_145_out, nand_146_out, nand_147_out, nand_148_out, nand_149_out,
       nand_150_out, nand_151_out, nand_152_out, nand_153_out, nand_154_out, nand_155_out, nand_156_out,
       nand_157_out, nand_158_out, nand_159_out, nand_160_out, nand_161_out, nand_162_out, nand_163_out,
       nand_164_out, nand_165_out, nand_166_out, nand_167_out, nand_168_out, nand_169_out, nand_170_out,
       nand_171_out, nand_172_out, nand_173_out, nand_174_out, nand_175_out, nand_176_out, nand_177_out,
       nand_178_out, nand_179_out, nand_180_out, nand_181_out, nand_182_out, nand_183_out, nand_184_out,
       nand_185_out, nand_186_out, nand_187_out, nand_188_out, nand_189_out, nand_190_out, nand_191_out,
       nand_192_out, nand_193_out, nand_194_out, nand_195_out, nand_196_out, nand_197_out, nand_198_out,
       nand_199_out, nand_200_out, nand_201_out, nand_202_out, nand_203_out, nand_204_out, nand_205_out,
       nand_206_out, nand_207_out, nand_208_out, nand_209_out, nand_210_out, nand_211_out, nand_212_out,
       nand_213_out, nand_214_out, nand_215_out, nand_216_out, nand_217_out, nand_218_out, nand_219_out,
       nand_220_out, nand_221_out, nand_222_out, nand_223_out, nand_224_out, nand_225_out, nand_226_out,
       nand_227_out, nand_228_out, nand_229_out, nand_230_out, nand_231_out, nand_232_out, nand_233_out,
       nand_234_out, nand_235_out, nand_236_out, nand_237_out, nand_238_out, nand_239_out, nand_240_out,
       nand_241_out, nand_242_out, nand_243_out, nand_244_out, nand_245_out, nand_246_out, nand_247_out,
       nand_248_out, nand_249_out, nand_250_out, nand_251_out, nand_252_out, nand_253_out, nand_254_out,
       nand_255_out, nand_256_out, nand_257_out, nand_258_out, nand_259_out, nand_260_out, nand_261_out,
       nand_262_out, nand_263_out, nand_264_out, nand_265_out, nand_266_out, nand_267_out, nand_268_out,
       nand_269_out, nand_270_out, nand_271_out, nand_272_out, nand_273_out, nand_274_out, nand_275_out,
       nand_276_out, nand_277_out, nand_278_out, nand_279_out, nand_280_out, nand_281_out, nand_282_out,
       nand_283_out, nand_284_out, nand_285_out, nand_286_out, nand_287_out, nand_288_out, nand_289_out,
       nand_290_out, nand_291_out, nand_292_out, nand_293_out, nand_294_out, nand_295_out, nand_296_out,
       nand_297_out, nand_298_out, nand_299_out, nand_300_out, nand_301_out, nand_302_out, nand_303_out,
       nand_304_out, nand_305_out, nand_306_out, nand_307_out, nand_308_out, nand_309_out, nand_310_out,
       nand_311_out, nand_312_out, nand_313_out, nand_314_out, nand_315_out, nand_316_out, nand_317_out,
       nand_318_out, nand_319_out, nand_320_out, nand_321_out, nand_322_out, nand_323_out, nand_324_out,
       nand_325_out, nand_326_out, nand_327_out, nand_328_out, nand_329_out, nand_330_out, nand_331_out,
       nand_332_out, nand_333_out, nand_334_out, nand_335_out, nand_336_out, nand_337_out, nand_338_out,
       nand_339_out, nand_340_out, nand_341_out, nand_342_out, nand_343_out, nand_344_out, nand_345_out,
       nand_346_out, nand_347_out, nand_348_out, nand_349_out, nand_350_out, nand_357_out, nand_358_out,
       nand_359_out, nand_360_out;

  nand nand_1 (nand_1_out, i[2], i[2]);
  nand nand_2 (nand_2_out, i[1], i[1]);
  nand nand_3 (nand_3_out, i[4], i[4]);
  nand nand_4 (nand_4_out, i[3], i[3]);
  nand nand_5 (nand_5_out, i[4], i[4]);
  nand nand_6 (nand_6_out, i[3], i[3]);
  nand nand_7 (nand_7_out, i[4], i[4]);
  nand nand_8 (nand_8_out, i[2], i[2]);
  nand nand_9 (nand_9_out, i[2], i[2]);
  nand nand_10 (nand_10_out, i[4], i[4]);
  nand nand_11 (nand_11_out, i[3], i[3]);
  nand nand_12 (nand_12_out, i[1], i[1]);
  nand nand_13 (nand_13_out, i[0], i[0]);
  nand nand_14 (nand_14_out, i[4], i[4]);
  nand nand_15 (nand_15_out, i[2], i[2]);
  nand nand_16 (nand_16_out, i[3], i[3]);
  nand nand_17 (nand_17_out, i[2], i[2]);
  nand nand_18 (nand_18_out, i[4], i[4]);
  nand nand_19 (nand_19_out, i[3], i[3]);
  nand nand_20 (nand_20_out, i[2], i[2]);
  nand nand_21 (nand_21_out, i[4], i[4]);
  nand nand_22 (nand_22_out, i[1], i[1]);
  nand nand_23 (nand_23_out, i[4], i[4]);
  nand nand_24 (nand_24_out, i[3], i[3]);
  nand nand_25 (nand_25_out, i[4], i[4]);
  nand nand_26 (nand_26_out, i[3], i[3]);
  nand nand_27 (nand_27_out, i[4], i[4]);
  nand nand_28 (nand_28_out, i[1], i[1]);
  nand nand_29 (nand_29_out, i[4], i[4]);
  nand nand_30 (nand_30_out, i[3], i[3]);
  nand nand_31 (nand_31_out, i[4], i[4]);
  nand nand_32 (nand_32_out, i[3], i[3]);
  nand nand_33 (nand_33_out, i[2], i[2]);
  nand nand_34 (nand_34_out, i[1], i[1]);
  nand nand_35 (nand_35_out, i[4], i[4]);
  nand nand_36 (nand_36_out, i[3], i[3]);
  nand nand_37 (nand_37_out, i[0], i[0]);
  nand nand_38 (nand_38_out, i[3], i[3]);
  nand nand_39 (nand_39_out, i[2], i[2]);
  nand nand_40 (nand_40_out, i[4], i[4]);
  nand nand_41 (nand_41_out, i[1], i[1]);
  nand nand_42 (nand_42_out, i[4], i[4]);
  nand nand_43 (nand_43_out, i[4], i[4]);
  nand nand_44 (nand_44_out, i[2], i[2]);
  nand nand_45 (nand_45_out, i[3], i[3]);
  nand nand_46 (nand_46_out, i[1], i[1]);
  nand nand_47 (nand_47_out, i[4], i[4]);
  nand nand_48 (nand_48_out, i[2], i[2]);
  nand nand_49 (nand_49_out, i[2], i[2]);
  nand nand_50 (nand_50_out, i[1], i[1]);
  nand nand_51 (nand_51_out, i[4], i[4]);
  nand nand_52 (nand_52_out, i[4], i[4]);
  nand nand_53 (nand_53_out, i[4], i[4]);
  nand nand_54 (nand_54_out, i[3], i[3]);
  nand nand_55 (nand_55_out, i[3], i[3]);
  nand nand_56 (nand_56_out, i[4], i[4]);
  nand nand_57 (nand_57_out, i[4], i[4]);
  nand nand_58 (nand_58_out, i[2], i[2]);
  nand nand_59 (nand_59_out, i[4], i[4]);
  nand nand_60 (nand_60_out, nand_1_out, nand_2_out);
  nand nand_61 (nand_61_out, nand_3_out, nand_4_out);
  nand nand_62 (nand_62_out, nand_5_out, nand_6_out);
  nand nand_63 (nand_63_out, i[2], i[0]);
  nand nand_64 (nand_64_out, nand_7_out, i[2]);
  nand nand_65 (nand_65_out, i[3], nand_8_out);
  nand nand_66 (nand_66_out, i[3], nand_9_out);
  nand nand_67 (nand_67_out, nand_10_out, nand_11_out);
  nand nand_68 (nand_68_out, nand_12_out, nand_13_out);
  nand nand_69 (nand_69_out, nand_14_out, nand_15_out);
  nand nand_70 (nand_70_out, nand_16_out, nand_17_out);
  nand nand_71 (nand_71_out, nand_18_out, nand_19_out);
  nand nand_72 (nand_72_out, i[1], i[0]);
  nand nand_73 (nand_73_out, i[3], nand_20_out);
  nand nand_74 (nand_74_out, nand_21_out, i[3]);
  nand nand_75 (nand_75_out, nand_22_out, i[0]);
  nand nand_76 (nand_76_out, i[4], i[1]);
  nand nand_77 (nand_77_out, i[4], i[3]);
  nand nand_78 (nand_78_out, i[2], i[1]);
  nand nand_79 (nand_79_out, nand_23_out, nand_24_out);
  nand nand_80 (nand_80_out, nand_25_out, nand_26_out);
  nand nand_81 (nand_81_out, nand_27_out, nand_28_out);
  nand nand_82 (nand_82_out, nand_29_out, nand_30_out);
  nand nand_83 (nand_83_out, nand_31_out, i[3]);
  nand nand_84 (nand_84_out, i[4], nand_32_out);
  nand nand_85 (nand_85_out, i[4], i[2]);
  nand nand_86 (nand_86_out, i[4], i[3]);
  nand nand_87 (nand_87_out, nand_33_out, nand_34_out);
  nand nand_88 (nand_88_out, nand_35_out, nand_36_out);
  nand nand_89 (nand_89_out, i[1], nand_37_out);
  nand nand_90 (nand_90_out, nand_38_out, nand_39_out);
  nand nand_91 (nand_91_out, i[1], i[0]);
  nand nand_92 (nand_92_out, nand_40_out, i[2]);
  nand nand_93 (nand_93_out, nand_41_out, i[0]);
  nand nand_94 (nand_94_out, nand_42_out, i[3]);
  nand nand_95 (nand_95_out, nand_43_out, i[3]);
  nand nand_96 (nand_96_out, nand_44_out, i[0]);
  nand nand_97 (nand_97_out, i[3], i[2]);
  nand nand_98 (nand_98_out, i[4], nand_45_out);
  nand nand_99 (nand_99_out, i[2], nand_46_out);
  nand nand_100 (nand_100_out, nand_47_out, nand_48_out);
  nand nand_101 (nand_101_out, nand_49_out, nand_50_out);
  nand nand_102 (nand_102_out, nand_51_out, i[1]);
  nand nand_103 (nand_103_out, nand_52_out, i[3]);
  nand nand_104 (nand_104_out, nand_53_out, i[3]);
  nand nand_105 (nand_105_out, i[4], nand_54_out);
  nand nand_106 (nand_106_out, i[4], i[2]);
  nand nand_107 (nand_107_out, i[4], i[3]);
  nand nand_108 (nand_108_out, nand_55_out, i[2]);
  nand nand_109 (nand_109_out, nand_56_out, i[3]);
  nand nand_110 (nand_110_out, i[3], i[2]);
  nand nand_111 (nand_111_out, nand_57_out, nand_58_out);
  nand nand_112 (nand_112_out, nand_59_out, i[2]);
  nand nand_113 (nand_113_out, nand_60_out, nand_60_out);
  nand nand_114 (nand_114_out, i[0], i[0]);
  nand nand_115 (nand_115_out, nand_61_out, nand_61_out);
  nand nand_116 (nand_116_out, nand_62_out, nand_62_out);
  nand nand_117 (nand_117_out, nand_63_out, nand_63_out);
  nand nand_118 (nand_118_out, nand_64_out, nand_64_out);
  nand nand_119 (nand_119_out, nand_65_out, nand_65_out);
  nand nand_120 (nand_120_out, i[1], i[1]);
  nand nand_121 (nand_121_out, nand_66_out, nand_66_out);
  nand nand_122 (nand_122_out, i[0], i[0]);
  nand nand_123 (nand_123_out, i[1], i[1]);
  nand nand_124 (nand_124_out, nand_67_out, nand_67_out);
  nand nand_125 (nand_125_out, nand_68_out, nand_68_out);
  nand nand_126 (nand_126_out, nand_69_out, nand_69_out);
  nand nand_127 (nand_127_out, i[0], i[0]);
  nand nand_128 (nand_128_out, nand_70_out, nand_70_out);
  nand nand_129 (nand_129_out, nand_71_out, nand_71_out);
  nand nand_130 (nand_130_out, nand_72_out, nand_72_out);
  nand nand_131 (nand_131_out, nand_73_out, nand_73_out);
  nand nand_132 (nand_132_out, i[1], i[1]);
  nand nand_133 (nand_133_out, nand_74_out, nand_74_out);
  nand nand_134 (nand_134_out, nand_75_out, nand_75_out);
  nand nand_135 (nand_135_out, nand_76_out, nand_76_out);
  nand nand_136 (nand_136_out, i[0], i[0]);
  nand nand_137 (nand_137_out, nand_77_out, nand_77_out);
  nand nand_138 (nand_138_out, nand_78_out, nand_78_out);
  nand nand_139 (nand_139_out, nand_79_out, nand_79_out);
  nand nand_140 (nand_140_out, i[1], i[1]);
  nand nand_141 (nand_141_out, nand_80_out, nand_80_out);
  nand nand_142 (nand_142_out, nand_81_out, nand_81_out);
  nand nand_143 (nand_143_out, nand_82_out, nand_82_out);
  nand nand_144 (nand_144_out, nand_83_out, nand_83_out);
  nand nand_145 (nand_145_out, i[2], i[2]);
  nand nand_146 (nand_146_out, nand_84_out, nand_84_out);
  nand nand_147 (nand_147_out, i[2], i[2]);
  nand nand_148 (nand_148_out, nand_85_out, nand_85_out);
  nand nand_149 (nand_149_out, nand_86_out, nand_86_out);
  nand nand_150 (nand_150_out, i[0], i[0]);
  nand nand_151 (nand_151_out, nand_87_out, nand_87_out);
  nand nand_152 (nand_152_out, i[0], i[0]);
  nand nand_153 (nand_153_out, nand_88_out, nand_88_out);
  nand nand_154 (nand_154_out, nand_89_out, nand_89_out);
  nand nand_155 (nand_155_out, nand_90_out, nand_90_out);
  nand nand_156 (nand_156_out, nand_91_out, nand_91_out);
  nand nand_157 (nand_157_out, nand_92_out, nand_92_out);
  nand nand_158 (nand_158_out, nand_93_out, nand_93_out);
  nand nand_159 (nand_159_out, nand_94_out, nand_94_out);
  nand nand_160 (nand_160_out, i[1], i[1]);
  nand nand_161 (nand_161_out, nand_95_out, nand_95_out);
  nand nand_162 (nand_162_out, nand_96_out, nand_96_out);
  nand nand_163 (nand_163_out, nand_97_out, nand_97_out);
  nand nand_164 (nand_164_out, i[0], i[0]);
  nand nand_165 (nand_165_out, nand_98_out, nand_98_out);
  nand nand_166 (nand_166_out, nand_99_out, nand_99_out);
  nand nand_167 (nand_167_out, nand_100_out, nand_100_out);
  nand nand_168 (nand_168_out, i[0], i[0]);
  nand nand_169 (nand_169_out, nand_101_out, nand_101_out);
  nand nand_170 (nand_170_out, i[0], i[0]);
  nand nand_171 (nand_171_out, nand_102_out, nand_102_out);
  nand nand_172 (nand_172_out, i[0], i[0]);
  nand nand_173 (nand_173_out, nand_103_out, nand_103_out);
  nand nand_174 (nand_174_out, nand_104_out, nand_104_out);
  nand nand_175 (nand_175_out, nand_105_out, nand_105_out);
  nand nand_176 (nand_176_out, i[1], i[1]);
  nand nand_177 (nand_177_out, nand_106_out, nand_106_out);
  nand nand_178 (nand_178_out, nand_107_out, nand_107_out);
  nand nand_179 (nand_179_out, i[1], i[1]);
  nand nand_180 (nand_180_out, i[0], i[0]);
  nand nand_181 (nand_181_out, nand_108_out, nand_108_out);
  nand nand_182 (nand_182_out, i[1], i[1]);
  nand nand_183 (nand_183_out, i[0], i[0]);
  nand nand_184 (nand_184_out, nand_109_out, nand_109_out);
  nand nand_185 (nand_185_out, i[2], i[2]);
  nand nand_186 (nand_186_out, i[0], i[0]);
  nand nand_187 (nand_187_out, nand_110_out, nand_110_out);
  nand nand_188 (nand_188_out, nand_111_out, nand_111_out);
  nand nand_189 (nand_189_out, nand_112_out, nand_112_out);
  nand nand_190 (nand_190_out, i[1], i[1]);
  nand nand_191 (nand_191_out, i[3], i[3]);
  nand nand_192 (nand_192_out, i[1], i[1]);
  nand nand_193 (nand_193_out, i[2], i[2]);
  nand nand_194 (nand_194_out, i[2], i[2]);
  nand nand_195 (nand_195_out, i[1], i[1]);
  nand nand_196 (nand_196_out, i[3], i[3]);
  nand nand_197 (nand_197_out, nand_113_out, nand_114_out);
  nand nand_198 (nand_198_out, nand_115_out, i[1]);
  nand nand_199 (nand_199_out, nand_116_out, nand_117_out);
  nand nand_200 (nand_200_out, nand_118_out, i[1]);
  nand nand_201 (nand_201_out, nand_119_out, nand_120_out);
  nand nand_202 (nand_202_out, nand_121_out, nand_122_out);
  nand nand_203 (nand_203_out, i[3], nand_123_out);
  nand nand_204 (nand_204_out, nand_124_out, nand_125_out);
  nand nand_205 (nand_205_out, nand_126_out, nand_127_out);
  nand nand_206 (nand_206_out, nand_128_out, i[0]);
  nand nand_207 (nand_207_out, nand_129_out, nand_130_out);
  nand nand_208 (nand_208_out, nand_131_out, nand_132_out);
  nand nand_209 (nand_209_out, nand_133_out, nand_134_out);
  nand nand_210 (nand_210_out, nand_135_out, nand_136_out);
  nand nand_211 (nand_211_out, nand_137_out, nand_138_out);
  nand nand_212 (nand_212_out, nand_139_out, nand_140_out);
  nand nand_213 (nand_213_out, nand_141_out, i[0]);
  nand nand_214 (nand_214_out, nand_142_out, i[0]);
  nand nand_215 (nand_215_out, nand_143_out, i[2]);
  nand nand_216 (nand_216_out, nand_144_out, nand_145_out);
  nand nand_217 (nand_217_out, nand_146_out, nand_147_out);
  nand nand_218 (nand_218_out, nand_148_out, i[1]);
  nand nand_219 (nand_219_out, nand_149_out, nand_150_out);
  nand nand_220 (nand_220_out, nand_151_out, nand_152_out);
  nand nand_221 (nand_221_out, nand_153_out, nand_154_out);
  nand nand_222 (nand_222_out, nand_155_out, nand_156_out);
  nand nand_223 (nand_223_out, nand_157_out, nand_158_out);
  nand nand_224 (nand_224_out, nand_159_out, nand_160_out);
  nand nand_225 (nand_225_out, nand_161_out, nand_162_out);
  nand nand_226 (nand_226_out, nand_163_out, nand_164_out);
  nand nand_227 (nand_227_out, nand_165_out, nand_166_out);
  nand nand_228 (nand_228_out, nand_167_out, nand_168_out);
  nand nand_229 (nand_229_out, nand_169_out, nand_170_out);
  nand nand_230 (nand_230_out, nand_171_out, nand_172_out);
  nand nand_231 (nand_231_out, nand_173_out, i[1]);
  nand nand_232 (nand_232_out, nand_174_out, i[2]);
  nand nand_233 (nand_233_out, nand_175_out, nand_176_out);
  nand nand_234 (nand_234_out, nand_177_out, i[1]);
  nand nand_235 (nand_235_out, nand_178_out, i[0]);
  nand nand_236 (nand_236_out, nand_179_out, nand_180_out);
  nand nand_237 (nand_237_out, nand_181_out, nand_182_out);
  nand nand_238 (nand_238_out, i[2], nand_183_out);
  nand nand_239 (nand_239_out, nand_184_out, nand_185_out);
  nand nand_240 (nand_240_out, i[3], nand_186_out);
  nand nand_241 (nand_241_out, nand_187_out, i[1]);
  nand nand_242 (nand_242_out, nand_188_out, i[1]);
  nand nand_243 (nand_243_out, nand_189_out, nand_190_out);
  nand nand_244 (nand_244_out, nand_191_out, i[2]);
  nand nand_245 (nand_245_out, i[2], nand_192_out);
  nand nand_246 (nand_246_out, i[3], nand_193_out);
  nand nand_247 (nand_247_out, i[4], nand_194_out);
  nand nand_248 (nand_248_out, nand_195_out, i[0]);
  nand nand_249 (nand_249_out, i[4], nand_196_out);
  nand nand_250 (nand_250_out, i[2], i[1]);
  nand nand_251 (nand_251_out, nand_197_out, nand_198_out);
  nand nand_252 (nand_252_out, nand_199_out, nand_200_out);
  nand nand_253 (nand_253_out, nand_201_out, nand_202_out);
  nand nand_254 (nand_254_out, nand_203_out, nand_203_out);
  nand nand_255 (nand_255_out, i[0], i[0]);
  nand nand_256 (nand_256_out, nand_204_out, nand_205_out);
  nand nand_257 (nand_257_out, nand_206_out, nand_207_out);
  nand nand_258 (nand_258_out, nand_208_out, nand_209_out);
  nand nand_259 (nand_259_out, nand_210_out, nand_211_out);
  nand nand_260 (nand_260_out, nand_212_out, nand_213_out);
  nand nand_261 (nand_261_out, nand_214_out, nand_215_out);
  nand nand_262 (nand_262_out, nand_216_out, nand_217_out);
  nand nand_263 (nand_263_out, nand_218_out, nand_219_out);
  nand nand_264 (nand_264_out, nand_220_out, nand_221_out);
  nand nand_265 (nand_265_out, nand_222_out, nand_223_out);
  nand nand_266 (nand_266_out, nand_224_out, nand_225_out);
  nand nand_267 (nand_267_out, nand_226_out, nand_227_out);
  nand nand_268 (nand_268_out, nand_228_out, nand_229_out);
  nand nand_269 (nand_269_out, nand_230_out, nand_231_out);
  nand nand_270 (nand_270_out, nand_232_out, nand_233_out);
  nand nand_271 (nand_271_out, nand_234_out, nand_235_out);
  nand nand_272 (nand_272_out, nand_236_out, nand_237_out);
  nand nand_273 (nand_273_out, nand_238_out, nand_239_out);
  nand nand_274 (nand_274_out, nand_240_out, nand_241_out);
  nand nand_275 (nand_275_out, i[1], i[1]);
  nand nand_276 (nand_276_out, nand_242_out, nand_243_out);
  nand nand_277 (nand_277_out, nand_244_out, nand_244_out);
  nand nand_278 (nand_278_out, i[0], i[0]);
  nand nand_279 (nand_279_out, nand_245_out, nand_245_out);
  nand nand_280 (nand_280_out, i[0], i[0]);
  nand nand_281 (nand_281_out, i[4], i[4]);
  nand nand_282 (nand_282_out, nand_246_out, nand_246_out);
  nand nand_283 (nand_283_out, nand_247_out, nand_247_out);
  nand nand_284 (nand_284_out, nand_248_out, nand_248_out);
  nand nand_285 (nand_285_out, nand_249_out, nand_249_out);
  nand nand_286 (nand_286_out, nand_250_out, nand_250_out);
  nand nand_287 (nand_287_out, nand_251_out, nand_251_out);
  nand nand_288 (nand_288_out, nand_252_out, nand_252_out);
  nand nand_289 (nand_289_out, nand_253_out, nand_253_out);
  nand nand_290 (nand_290_out, nand_254_out, nand_255_out);
  nand nand_291 (nand_291_out, nand_256_out, nand_256_out);
  nand nand_292 (nand_292_out, nand_257_out, nand_257_out);
  nand nand_293 (nand_293_out, nand_258_out, nand_258_out);
  nand nand_294 (nand_294_out, nand_259_out, nand_259_out);
  nand nand_295 (nand_295_out, nand_260_out, nand_260_out);
  nand nand_296 (nand_296_out, nand_261_out, nand_261_out);
  nand nand_297 (nand_297_out, nand_262_out, nand_262_out);
  nand nand_298 (nand_298_out, nand_263_out, nand_263_out);
  nand nand_299 (nand_299_out, nand_264_out, nand_264_out);
  nand nand_300 (nand_300_out, nand_265_out, nand_265_out);
  nand nand_301 (nand_301_out, nand_266_out, nand_266_out);
  nand nand_302 (nand_302_out, nand_267_out, nand_267_out);
  nand nand_303 (nand_303_out, nand_268_out, nand_268_out);
  nand nand_304 (nand_304_out, nand_269_out, nand_269_out);
  nand nand_305 (nand_305_out, nand_270_out, nand_270_out);
  nand nand_306 (nand_306_out, nand_271_out, nand_271_out);
  nand nand_307 (nand_307_out, nand_272_out, nand_272_out);
  nand nand_308 (nand_308_out, nand_273_out, nand_273_out);
  nand nand_309 (nand_309_out, nand_274_out, nand_274_out);
  nand nand_310 (nand_310_out, i[4], nand_275_out);
  nand nand_311 (nand_311_out, nand_276_out, nand_276_out);
  nand nand_312 (nand_312_out, nand_277_out, nand_278_out);
  nand nand_313 (nand_313_out, nand_279_out, nand_280_out);
  nand nand_314 (nand_314_out, nand_281_out, i[3]);
  nand nand_315 (nand_315_out, i[3], i[0]);
  nand nand_316 (nand_316_out, nand_282_out, i[1]);
  nand nand_317 (nand_317_out, nand_283_out, nand_284_out);
  nand nand_318 (nand_318_out, nand_285_out, nand_286_out);
  nand nand_319 (nand_319_out, nand_287_out, nand_288_out);
  nand nand_320 (nand_320_out, nand_289_out, nand_290_out);
  nand nand_321 (nand_321_out, nand_291_out, nand_292_out);
  nand nand_322 (nand_322_out, nand_293_out, nand_294_out);
  nand nand_323 (nand_323_out, nand_295_out, nand_296_out);
  nand nand_324 (nand_324_out, nand_297_out, nand_298_out);
  nand nand_325 (nand_325_out, nand_299_out, nand_300_out);
  nand nand_326 (nand_326_out, nand_301_out, nand_302_out);
  nand nand_327 (nand_327_out, nand_303_out, nand_304_out);
  nand nand_328 (nand_328_out, nand_305_out, nand_306_out);
  nand nand_329 (nand_329_out, nand_307_out, nand_308_out);
  nand nand_330 (nand_330_out, nand_309_out, nand_310_out);
  nand nand_331 (nand_331_out, nand_311_out, nand_312_out);
  nand nand_332 (nand_332_out, nand_313_out, nand_314_out);
  nand nand_333 (nand_333_out, nand_315_out, nand_316_out);
  nand nand_334 (nand_334_out, nand_317_out, nand_318_out);
  nand nand_335 (nand_335_out, nand_319_out, nand_319_out);
  nand nand_336 (nand_336_out, nand_320_out, nand_320_out);
  nand nand_337 (nand_337_out, nand_321_out, nand_321_out);
  nand nand_338 (nand_338_out, nand_322_out, nand_322_out);
  nand nand_339 (nand_339_out, nand_323_out, nand_323_out);
  nand nand_340 (nand_340_out, nand_324_out, nand_324_out);
  nand nand_341 (nand_341_out, nand_325_out, nand_325_out);
  nand nand_342 (nand_342_out, nand_326_out, nand_326_out);
  nand nand_343 (nand_343_out, nand_327_out, nand_327_out);
  nand nand_344 (nand_344_out, nand_328_out, nand_328_out);
  nand nand_345 (nand_345_out, nand_329_out, nand_329_out);
  nand nand_346 (nand_346_out, nand_330_out, nand_330_out);
  nand nand_347 (nand_347_out, nand_331_out, nand_331_out);
  nand nand_348 (nand_348_out, nand_332_out, nand_332_out);
  nand nand_349 (nand_349_out, nand_333_out, nand_333_out);
  nand nand_350 (nand_350_out, nand_334_out, nand_334_out);
  nand nand_351 (a, nand_335_out, nand_336_out);
  nand nand_352 (b, nand_337_out, nand_338_out);
  nand nand_353 (c, nand_339_out, nand_340_out);
  nand nand_354 (d, nand_341_out, nand_342_out);
  nand nand_355 (e, nand_343_out, nand_344_out);
  nand nand_356 (f, nand_345_out, nand_346_out);
  nand nand_357 (nand_357_out, nand_347_out, nand_348_out);
  nand nand_358 (nand_358_out, nand_349_out, nand_350_out);
  nand nand_359 (nand_359_out, nand_357_out, nand_357_out);
  nand nand_360 (nand_360_out, nand_358_out, nand_358_out);
  nand nand_361 (g, nand_359_out, nand_360_out);

  assign p = point;
endmodule

module transition_logic_half (
  input  C_3,
  input  C_2,
  input  C_1,
  input  C_0,
  input  B_1,
  input  B_0,
  output S_3,
  output S_2,
  output S_1,
  output S_0
);

  wire nand_1_out, nand_2_out, nand_3_out, nand_4_out, nand_5_out, nand_6_out, nand_7_out, nand_8_out,
       nand_9_out, nand_10_out, nand_11_out, nand_12_out, nand_13_out, nand_14_out, nand_15_out, nand_16_out,
       nand_17_out, nand_18_out, nand_19_out, nand_20_out, nand_21_out, nand_22_out, nand_23_out,
       nand_24_out, nand_25_out, nand_26_out, nand_27_out, nand_28_out, nand_29_out, nand_30_out,
       nand_31_out, nand_32_out, nand_33_out, nand_34_out, nand_35_out, nand_36_out, nand_37_out,
       nand_38_out, nand_39_out, nand_40_out, nand_41_out, nand_42_out, nand_43_out, nand_44_out,
       nand_45_out, nand_46_out, nand_47_out, nand_48_out, nand_49_out, nand_50_out, nand_51_out,
       nand_52_out, nand_53_out, nand_54_out, nand_55_out, nand_56_out, nand_57_out, nand_58_out,
       nand_59_out, nand_60_out, nand_61_out, nand_62_out, nand_63_out, nand_64_out, nand_65_out,
       nand_66_out, nand_67_out, nand_68_out, nand_69_out, nand_70_out, nand_71_out, nand_72_out,
       nand_73_out, nand_74_out, nand_75_out, nand_76_out, nand_77_out, nand_78_out, nand_79_out,
       nand_80_out, nand_81_out, nand_82_out, nand_83_out, nand_84_out, nand_85_out, nand_86_out,
       nand_87_out, nand_88_out, nand_89_out, nand_90_out, nand_91_out, nand_92_out, nand_93_out,
       nand_94_out, nand_95_out, nand_96_out, nand_97_out, nand_98_out, nand_99_out, nand_100_out,
       nand_101_out, nand_102_out, nand_103_out, nand_104_out, nand_105_out, nand_106_out, nand_107_out,
       nand_108_out, nand_109_out, nand_110_out, nand_112_out, nand_113_out, nand_114_out, nand_115_out;

  nand nand_1 (nand_1_out, C_2, C_2);
  nand nand_2 (nand_2_out, C_1, C_1);
  nand nand_3 (nand_3_out, C_0, C_0);
  nand nand_4 (nand_4_out, B_1, B_1);
  nand nand_5 (nand_5_out, B_1, B_1);
  nand nand_6 (nand_6_out, nand_1_out, C_1);
  nand nand_7 (nand_7_out, C_2, nand_2_out);
  nand nand_8 (nand_8_out, nand_3_out, nand_4_out);
  nand nand_9 (nand_9_out, C_0, nand_5_out);
  nand nand_10 (nand_10_out, C_1, C_0);
  nand nand_11 (nand_11_out, C_2, C_0);
  nand nand_12 (nand_12_out, nand_6_out, nand_6_out);
  nand nand_13 (nand_13_out, C_0, C_0);
  nand nand_14 (nand_14_out, B_0, B_0);
  nand nand_15 (nand_15_out, C_3, C_3);
  nand nand_16 (nand_16_out, C_2, C_2);
  nand nand_17 (nand_17_out, B_0, B_0);
  nand nand_18 (nand_18_out, B_1, B_1);
  nand nand_19 (nand_19_out, C_3, C_3);
  nand nand_20 (nand_20_out, C_2, C_2);
  nand nand_21 (nand_21_out, nand_7_out, nand_7_out);
  nand nand_22 (nand_22_out, C_0, C_0);
  nand nand_23 (nand_23_out, B_0, B_0);
  nand nand_24 (nand_24_out, nand_8_out, nand_8_out);
  nand nand_25 (nand_25_out, nand_9_out, nand_9_out);
  nand nand_26 (nand_26_out, B_0, B_0);
  nand nand_27 (nand_27_out, nand_10_out, nand_10_out);
  nand nand_28 (nand_28_out, B_0, B_0);
  nand nand_29 (nand_29_out, nand_11_out, nand_11_out);
  nand nand_30 (nand_30_out, B_0, B_0);
  nand nand_31 (nand_31_out, B_0, B_0);
  nand nand_32 (nand_32_out, nand_12_out, nand_13_out);
  nand nand_33 (nand_33_out, B_1, nand_14_out);
  nand nand_34 (nand_34_out, nand_15_out, C_2);
  nand nand_35 (nand_35_out, nand_16_out, C_0);
  nand nand_36 (nand_36_out, B_1, nand_17_out);
  nand nand_37 (nand_37_out, C_1, nand_18_out);
  nand nand_38 (nand_38_out, nand_19_out, C_1);
  nand nand_39 (nand_39_out, nand_20_out, C_1);
  nand nand_40 (nand_40_out, nand_21_out, nand_22_out);
  nand nand_41 (nand_41_out, B_1, nand_23_out);
  nand nand_42 (nand_42_out, nand_24_out, B_0);
  nand nand_43 (nand_43_out, nand_25_out, nand_26_out);
  nand nand_44 (nand_44_out, C_0, B_1);
  nand nand_45 (nand_45_out, nand_27_out, nand_28_out);
  nand nand_46 (nand_46_out, nand_29_out, nand_30_out);
  nand nand_47 (nand_47_out, C_2, C_1);
  nand nand_48 (nand_48_out, B_1, nand_31_out);
  nand nand_49 (nand_49_out, nand_32_out, nand_32_out);
  nand nand_50 (nand_50_out, nand_33_out, nand_33_out);
  nand nand_51 (nand_51_out, C_1, C_1);
  nand nand_52 (nand_52_out, B_1, B_1);
  nand nand_53 (nand_53_out, nand_34_out, nand_34_out);
  nand nand_54 (nand_54_out, nand_35_out, nand_35_out);
  nand nand_55 (nand_55_out, nand_36_out, nand_36_out);
  nand nand_56 (nand_56_out, nand_37_out, nand_37_out);
  nand nand_57 (nand_57_out, B_0, B_0);
  nand nand_58 (nand_58_out, nand_38_out, nand_38_out);
  nand nand_59 (nand_59_out, nand_39_out, nand_39_out);
  nand nand_60 (nand_60_out, nand_40_out, nand_40_out);
  nand nand_61 (nand_61_out, nand_41_out, nand_41_out);
  nand nand_62 (nand_62_out, nand_42_out, nand_43_out);
  nand nand_63 (nand_63_out, nand_44_out, nand_44_out);
  nand nand_64 (nand_64_out, nand_45_out, nand_46_out);
  nand nand_65 (nand_65_out, nand_47_out, nand_47_out);
  nand nand_66 (nand_66_out, nand_48_out, nand_48_out);
  nand nand_67 (nand_67_out, nand_49_out, nand_50_out);
  nand nand_68 (nand_68_out, C_2, nand_51_out);
  nand nand_69 (nand_69_out, C_2, nand_52_out);
  nand nand_70 (nand_70_out, nand_53_out, B_0);
  nand nand_71 (nand_71_out, C_2, C_0);
  nand nand_72 (nand_72_out, C_3, C_2);
  nand nand_73 (nand_73_out, nand_54_out, nand_55_out);
  nand nand_74 (nand_74_out, nand_56_out, nand_57_out);
  nand nand_75 (nand_75_out, nand_58_out, B_0);
  nand nand_76 (nand_76_out, nand_59_out, B_0);
  nand nand_77 (nand_77_out, C_1, C_0);
  nand nand_78 (nand_78_out, nand_60_out, nand_61_out);
  nand nand_79 (nand_79_out, C_3, C_2);
  nand nand_80 (nand_80_out, C_1, B_1);
  nand nand_81 (nand_81_out, nand_62_out, nand_62_out);
  nand nand_82 (nand_82_out, nand_63_out, B_0);
  nand nand_83 (nand_83_out, nand_64_out, nand_64_out);
  nand nand_84 (nand_84_out, nand_65_out, nand_66_out);
  nand nand_85 (nand_85_out, nand_67_out, nand_68_out);
  nand nand_86 (nand_86_out, nand_69_out, nand_69_out);
  nand nand_87 (nand_87_out, B_0, B_0);
  nand nand_88 (nand_88_out, nand_70_out, nand_71_out);
  nand nand_89 (nand_89_out, nand_72_out, nand_72_out);
  nand nand_90 (nand_90_out, nand_73_out, nand_74_out);
  nand nand_91 (nand_91_out, nand_75_out, nand_76_out);
  nand nand_92 (nand_92_out, nand_77_out, nand_78_out);
  nand nand_93 (nand_93_out, nand_79_out, nand_79_out);
  nand nand_94 (nand_94_out, nand_80_out, nand_80_out);
  nand nand_95 (nand_95_out, nand_81_out, nand_82_out);
  nand nand_96 (nand_96_out, nand_83_out, nand_84_out);
  nand nand_97 (nand_97_out, nand_85_out, nand_85_out);
  nand nand_98 (nand_98_out, nand_86_out, nand_87_out);
  nand nand_99 (nand_99_out, nand_88_out, nand_88_out);
  nand nand_100 (nand_100_out, nand_89_out, B_1);
  nand nand_101 (nand_101_out, nand_90_out, nand_90_out);
  nand nand_102 (nand_102_out, nand_91_out, nand_91_out);
  nand nand_103 (nand_103_out, nand_92_out, nand_92_out);
  nand nand_104 (nand_104_out, nand_93_out, nand_94_out);
  nand nand_105 (nand_105_out, nand_95_out, nand_95_out);
  nand nand_106 (nand_106_out, nand_96_out, nand_96_out);
  nand nand_107 (nand_107_out, nand_97_out, nand_98_out);
  nand nand_108 (nand_108_out, nand_99_out, nand_100_out);
  nand nand_109 (nand_109_out, nand_101_out, nand_102_out);
  nand nand_110 (nand_110_out, nand_103_out, nand_104_out);
  nand nand_111 (S_0, nand_105_out, nand_106_out);
  nand nand_112 (nand_112_out, nand_107_out, nand_107_out);
  nand nand_113 (nand_113_out, nand_108_out, nand_108_out);
  nand nand_114 (nand_114_out, nand_109_out, nand_109_out);
  nand nand_115 (nand_115_out, nand_110_out, nand_110_out);
  nand nand_116 (S_2, nand_112_out, nand_113_out);
  nand nand_117 (S_1, nand_114_out, nand_115_out);

  assign S_3 = 1'b0;
endmodule

module memory_time (
  input  [5:0] set_hour,
  input  [5:0] set_min,
  input  [5:0] set_sec,
  input  clock,
  input  reset,
  input  load,
  output carry,
  output [5:0] h_out,
  output [5:0] m_out,
  output [5:0] s_out
);

  wire shift_register_1_p3, shift_register_2_p3, shift_register_2_p4, shift_register_3_p3,
       shift_register_3_p4;

  // Shift_Register #(.length(2)) shift_register_1: pin names not known; wires that end beside it: reset, clock, shift_register_1_p3, carry
  Counter #(.width(6), .max('h17)) counter_1 (
    .clr(reset), .clk(shift_register_2_p4), .D(set_hour), .Q(h_out));  // open: load, up, count, carry
  Counter #(.width(6), .max('h3b)) counter_2 (
    .clr(reset), .clk(shift_register_3_p4), .D(set_min), .Q(m_out));  // open: load, up, count, carry
  Counter #(.width(6), .max('h3b)) counter_3 (
    .clr(reset), .load(load), .clk(clock), .D(set_sec), .Q(s_out));  // open: up, count, carry
  // Shift_Register #(.length(2)) shift_register_2: pin names not known; wires that end beside it: reset, clock, shift_register_2_p3, shift_register_2_p4
  // Shift_Register #(.length(2)) shift_register_3: pin names not known; wires that end beside it: reset, clock, shift_register_3_p3, shift_register_3_p4
  Comparator #(.width(6)) comparator_1 (.a(6'b111011), .b(m_out), .eq(shift_register_2_p3));  // open: gt, lt
  Comparator #(.width(6)) comparator_2 (.a(6'b010111), .b(h_out), .eq(shift_register_1_p3));  // open: gt, lt
  Comparator #(.width(6)) comparator_3 (.a(6'b111011), .b(s_out), .eq(shift_register_3_p3));  // open: gt, lt
endmodule

module inc_6bits (
  input  I_5,
  input  I_4,
  input  I_3,
  input  I_2,
  input  I_1,
  input  I_0,
  input  c_in,
  output c_out,
  output O_5,
  output O_4,
  output O_3,
  output O_2,
  output O_1,
  output O_0
);

  wire half_adder_2_ci, half_adder_3_ci, half_adder_4_ci, half_adder_5_ci, half_adder_6_ci;

  half_adder half_adder_1 (.ai(I_5), .bi(half_adder_2_ci), .si(O_5), .ci(c_out));
  half_adder half_adder_2 (.ai(I_4), .bi(half_adder_3_ci), .si(O_4), .ci(half_adder_2_ci));
  half_adder half_adder_3 (.ai(I_3), .bi(half_adder_4_ci), .si(O_3), .ci(half_adder_3_ci));
  half_adder half_adder_4 (.ai(I_2), .bi(half_adder_5_ci), .si(O_2), .ci(half_adder_4_ci));
  half_adder half_adder_5 (.ai(I_1), .bi(half_adder_6_ci), .si(O_1), .ci(half_adder_5_ci));
  half_adder half_adder_6 (.ai(I_0), .bi(c_in), .si(O_0), .ci(half_adder_6_ci));
endmodule

module half_adder (
  input  ai,
  input  bi,
  output si,
  output ci
);

  xor xor_1 (si, ai, bi);
  and and_1 (ci, ai, bi);
endmodule

module full_adder (
  input  ai,
  input  bi,
  input  ciminus1,
  output si,
  output ci
);

  wire and_4_out, nand_1_out, nand_2_out, nand_3_out, xor_1_out;

  xor xor_1 (xor_1_out, ai, bi);
  // AND_Gate and_1 has open pins: in0=ai, in1=bi, out=open
  nand nand_1 (nand_1_out, ai, bi);
  nand nand_2 (nand_2_out, ai, ciminus1);
  // AND_Gate and_2 has open pins: in0=ai, in1=ciminus1, out=open
  // AND_Gate and_3 has open pins: in0=bi, in1=ciminus1, out=open
  nand nand_3 (nand_3_out, bi, ciminus1);
  xor xor_2 (si, xor_1_out, ciminus1);
  and and_4 (and_4_out, nand_1_out, nand_2_out);
  nand nand_4 (ci, and_4_out, nand_3_out);
endmodule

module set_time_setter (
  input  [4:0] I_5,
  input  [4:0] I_4,
  input  [4:0] I_3,
  input  [4:0] I_2,
  input  [4:0] I_1,
  input  [4:0] I_0,
  input  [11:0] input_bus,
  input  [3:0] mode_on,
  input  R,
  output [4:0] O_5,
  output [4:0] O_4,
  output [4:0] O_3,
  output [4:0] O_2,
  output [4:0] O_1,
  output [4:0] O_0
);

  wire comparator_1_eq, not_1_out;

  Comparator #(.width(4)) comparator_1 (.a(mode_on), .b(4'b0011), .eq(comparator_1_eq));  // open: gt, lt
  not not_1 (not_1_out, comparator_1_eq);
  set_time_to_23 set_time_to_23_1 (
    .R(R), .B_1(input_bus[11]), .B_0(input_bus[10]), .load(not_1_out), .set_on(input_bus[4]), .I_1(I_5),
    .I_0(I_4), .O_1(O_5), .O_0(O_4));
  set_time_to_5 set_time_to_5_1 (
    .R(R), .B_1(input_bus[11]), .B_0(input_bus[10]), .load(not_1_out), .set_on(input_bus[3]), .I_0(I_3),
    .O_0(O_3));
  set_time_to_9 set_time_to_9_1 (
    .R(R), .B_1(input_bus[11]), .B_0(input_bus[10]), .load(not_1_out), .set_on(input_bus[2]), .I_0(I_2),
    .O_0(O_2));
  set_time_to_5 set_time_to_5_2 (
    .R(R), .B_1(input_bus[11]), .B_0(input_bus[10]), .load(not_1_out), .set_on(input_bus[1]), .I_0(I_1),
    .O_0(O_1));
  set_time_to_9 set_time_to_9_2 (
    .R(R), .B_1(input_bus[11]), .B_0(input_bus[10]), .load(not_1_out), .set_on(input_bus[0]), .I_0(I_0),
    .O_0(O_0));
endmodule

module set_time_to_9 (
  input  R,
  input  B_1,
  input  B_0,
  input  load,
  input  set_on,
  input  [4:0] I_0,
  output [4:0] O_0
);

  wire and_1_out, clock_1_out, or_1_out;

  Clock clock_1 (.out(clock_1_out));
  or or_1 (or_1_out, B_1, B_0);
  and and_1 (and_1_out, or_1_out, set_on);
  Counter #(.width(5), .max('h9)) counter_1 (
    .clr(R), .load(load), .up(B_0), .count(and_1_out), .clk(clock_1_out), .D(I_0), .Q(O_0));  // open: carry
endmodule

module alarme (
  input  [4:0] I_5,
  input  [4:0] I_4,
  input  [4:0] I_3,
  input  [4:0] I_2,
  input  [4:0] I_1,
  input  [4:0] I_0,
  input  B_1,
  input  B_0,
  input  DS_5,
  input  DS_4,
  input  DS_3,
  input  DS_2,
  input  DS_1,
  input  DS_0,
  input  R,
  output [4:0] O_5,
  output [4:0] O_4,
  output [4:0] O_3,
  output [4:0] O_2,
  output [4:0] O_1,
  output [4:0] O_0,
  output alarme
);

  wire clock_1_out, comparator_1_eq, comparator_2_eq, comparator_3_eq, comparator_4_eq, comparator_5_eq,
       comparator_6_eq;
  wire [4:0] register_1_q, register_2_q, register_3_q, register_4_q, register_5_q, register_6_q;

  Clock clock_1 (.out(clock_1_out));
  // set_time_setter set_time_setter_1: pin names not known; wires that end beside it: I_5, I_4, I_3, I_2, I_1, I_0, B_1, B_0, DS_5, DS_4, O_5, O_4, O_3, O_2, O_1, O_0
  Register #(.width(5)) register_1 (.D(O_5), .en(DS_5), .clk(clock_1_out), .Q(register_1_q), .clr(R));
  Register #(.width(5)) register_2 (.D(O_4), .en(DS_4), .clk(clock_1_out), .Q(register_2_q), .clr(R));
  Register #(.width(5)) register_3 (.D(O_3), .en(DS_3), .clk(clock_1_out), .Q(register_3_q), .clr(R));
  Register #(.width(5)) register_4 (.D(O_2), .en(DS_2), .clk(clock_1_out), .Q(register_4_q), .clr(R));
  Register #(.width(5)) register_5 (.D(O_1), .en(DS_1), .clk(clock_1_out), .Q(register_5_q), .clr(R));
  Register #(.width(5)) register_6 (.D(O_0), .en(DS_0), .clk(clock_1_out), .Q(register_6_q), .clr(R));
  Comparator #(.width(5)) comparator_1 (.a(register_1_q), .b(O_5), .eq(comparator_1_eq));  // open: gt, lt
  Comparator #(.width(5)) comparator_2 (.a(register_2_q), .b(O_4), .eq(comparator_2_eq));  // open: gt, lt
  Comparator #(.width(5)) comparator_3 (.a(register_3_q), .b(O_3), .eq(comparator_3_eq));  // open: gt, lt
  Comparator #(.width(5)) comparator_4 (.a(register_4_q), .b(O_2), .eq(comparator_4_eq));  // open: gt, lt
  Comparator #(.width(5)) comparator_5 (.a(register_5_q), .b(O_1), .eq(comparator_5_eq));  // open: gt, lt
  Comparator #(.width(5)) comparator_6 (.a(register_6_q), .b(O_0), .eq(comparator_6_eq));  // open: gt, lt
  and and_1 (alarme, comparator_1_eq, comparator_2_eq, comparator_3_eq, comparator_4_eq, comparator_5_eq, comparator_6_eq);
endmodule

module set_time_to_5 (
  input  R,
  input  B_1,
  input  B_0,
  input  load,
  input  set_on,
  input  [4:0] I_0,
  output [4:0] O_0
);

  wire and_1_out, C_out, or_1_out;

  Clock C (.out(C_out));
  or or_1 (or_1_out, B_1, B_0);
  and and_1 (and_1_out, or_1_out, set_on);
  Counter #(.width(5), .max('h5)) counter_1 (
    .clr(R), .load(load), .up(B_0), .count(and_1_out), .clk(C_out), .D(I_0), .Q(O_0));  // open: carry
endmodule

module set_time_to_23 (
  input  R,
  input  B_1,
  input  B_0,
  input  load,
  input  set_on,
  input  [4:0] I_1,
  input  [4:0] I_0,
  output [4:0] O_1,
  output [4:0] O_0
);

  wire and_1_out, and_2_out, and_3_out, and_4_out, and_5_out, C_out, comparator_1_eq, comparator_2_eq,
       counter_1_carry, counter_2_carry, d_ff_1_q, or_1_out, or_2_out, or_3_out, or_4_out;
  wire [4:0] multiplexer_1_out, multiplexer_2_out;

  Clock C (.out(C_out));
  or or_1 (or_1_out, B_1, B_0);
  and and_1 (and_1_out, or_1_out, set_on);
  or or_2 (or_2_out, counter_2_carry, and_4_out, and_2_out);
  D_Flip_Flop d_ff_1 (.D(or_2_out), .clk(C_out), .Q(d_ff_1_q), .reset(R));  // open: Qn, preset
  or or_3 (or_3_out, and_2_out, and_4_out);
  or or_4 (or_4_out, or_3_out, load);
  Multiplexer #(.width(5), .enable("false")) multiplexer_1 (
    .in0(I_0), .in1(multiplexer_2_out), .out(multiplexer_1_out), .sel(or_3_out));
  Multiplexer #(.width(5), .enable("false")) multiplexer_2 (
    .in0({5{1'b0}}), .in1(5'b00011), .out(multiplexer_2_out), .sel(and_4_out));
  Counter #(.width(5), .max('h2)) counter_1 (
    .clr(R), .load(load), .up(B_0), .count(or_1_out), .clk(d_ff_1_q), .D(I_1), .carry(counter_1_carry),
    .Q(O_1));
  and and_2 (and_2_out, counter_1_carry, and_3_out);
  and and_3 (and_3_out, comparator_2_eq, B_0);
  and and_4 (and_4_out, counter_1_carry, and_5_out);
  and and_5 (and_5_out, ~B_0, comparator_1_eq);  // AND_Gate
  Counter #(.width(5), .max('h9)) counter_2 (
    .clr(R), .load(or_4_out), .up(B_0), .count(and_1_out), .clk(C_out), .D(multiplexer_1_out),
    .carry(counter_2_carry), .Q(O_0));
  Comparator #(.width(5)) comparator_1 (.a({5{1'b0}}), .b(O_0), .eq(comparator_1_eq));  // open: gt, lt
  Comparator #(.width(5)) comparator_2 (.a(5'b00011), .b(O_0), .eq(comparator_2_eq));  // open: gt, lt
endmodule

module time_to_binary_converter (
  input  [5:0] t_in,
  output [4:0] O_1,
  output [4:0] O_0
);

  wire nand_1_out, nand_2_out, nand_3_out, nand_4_out, nand_5_out, nand_6_out, nand_7_out, nand_8_out,
       nand_9_out, nand_10_out, nand_11_out, nand_12_out, nand_13_out, nand_14_out, nand_15_out, nand_16_out,
       nand_17_out, nand_18_out, nand_19_out, nand_20_out, nand_21_out, nand_22_out, nand_23_out,
       nand_24_out, nand_25_out, nand_26_out, nand_27_out, nand_28_out, nand_29_out, nand_30_out,
       nand_31_out, nand_32_out, nand_33_out, nand_34_out, nand_35_out, nand_36_out, nand_37_out,
       nand_38_out, nand_39_out, nand_40_out, nand_41_out, nand_42_out, nand_43_out, nand_44_out,
       nand_45_out, nand_46_out, nand_47_out, nand_48_out, nand_49_out, nand_50_out, nand_51_out,
       nand_52_out, nand_53_out, nand_54_out, nand_56_out, nand_57_out, nand_58_out, nand_59_out,
       nand_60_out, nand_61_out, nand_62_out, nand_63_out, nand_64_out, nand_65_out, nand_66_out,
       nand_67_out, nand_68_out, nand_69_out, nand_70_out, nand_71_out, nand_72_out, nand_73_out,
       nand_74_out, nand_75_out, nand_76_out, nand_77_out, nand_78_out, nand_79_out, nand_80_out,
       nand_81_out, nand_82_out, nand_83_out, nand_84_out, nand_85_out, nand_86_out, nand_87_out,
       nand_88_out, nand_89_out, nand_90_out, nand_91_out, nand_92_out, nand_93_out, nand_94_out,
       nand_95_out, nand_96_out, nand_97_out, nand_98_out, nand_99_out, nand_100_out, nand_101_out,
       nand_102_out, nand_103_out, nand_104_out, nand_105_out, nand_106_out, nand_107_out, nand_108_out,
       nand_109_out, nand_110_out, nand_111_out, nand_112_out, nand_113_out, nand_114_out, nand_115_out,
       nand_116_out, nand_117_out, nand_118_out, nand_119_out, nand_120_out, nand_121_out, nand_122_out,
       nand_123_out, nand_124_out, nand_125_out, nand_126_out, nand_127_out, nand_128_out, nand_129_out,
       nand_130_out, nand_131_out, nand_132_out, nand_133_out, nand_134_out, nand_135_out, nand_136_out,
       nand_137_out, nand_138_out, nand_139_out, nand_140_out, nand_141_out, nand_142_out, nand_143_out,
       nand_144_out, nand_145_out, nand_146_out, nand_147_out, nand_148_out, nand_149_out, nand_150_out,
       nand_151_out, nand_152_out, nand_153_out, nand_154_out, nand_155_out, nand_156_out, nand_157_out,
       nand_158_out, nand_159_out, nand_160_out, nand_161_out, nand_162_out, nand_163_out, nand_164_out,
       nand_165_out, nand_166_out, nand_167_out, nand_168_out, nand_169_out, nand_170_out, nand_171_out,
       nand_172_out, nand_173_out, nand_174_out, nand_175_out, nand_176_out, nand_177_out, nand_178_out,
       nand_179_out, nand_180_out, nand_181_out, nand_182_out, nand_183_out, nand_184_out, nand_185_out,
       nand_186_out, nand_187_out, nand_188_out, nand_189_out, nand_190_out, nand_191_out, nand_192_out,
       nand_193_out, nand_194_out, nand_195_out, nand_196_out, nand_197_out, nand_198_out, nand_199_out,
       nand_200_out, nand_201_out, nand_202_out, nand_203_out, nand_204_out, nand_205_out, nand_206_out,
       nand_207_out, nand_208_out, nand_209_out, nand_210_out, nand_211_out, nand_212_out, nand_213_out,
       nand_214_out, nand_215_out, nand_216_out, nand_217_out, nand_218_out, nand_219_out, nand_220_out,
       nand_221_out, nand_222_out, nand_223_out, nand_224_out, nand_225_out, nand_226_out, nand_227_out,
       nand_228_out, nand_229_out, nand_230_out, nand_231_out, nand_232_out, nand_233_out, nand_234_out,
       nand_235_out, nand_236_out, nand_237_out, nand_238_out, nand_239_out, nand_240_out, nand_241_out,
       nand_242_out, nand_243_out, nand_244_out, nand_245_out, nand_246_out, nand_247_out, nand_248_out,
       nand_249_out, nand_250_out, nand_251_out, nand_252_out, nand_253_out, nand_254_out, nand_255_out,
       nand_256_out, nand_257_out, nand_258_out, nand_259_out, nand_260_out, nand_261_out, nand_262_out,
       nand_263_out, nand_264_out, nand_265_out, nand_266_out, nand_267_out, nand_268_out, nand_269_out,
       nand_270_out, nand_271_out, nand_272_out, nand_273_out, nand_274_out, nand_275_out, nand_276_out,
       nand_277_out, nand_278_out, nand_279_out, nand_280_out, nand_281_out, nand_282_out, nand_283_out,
       nand_284_out, nand_285_out, nand_286_out, nand_287_out, nand_288_out, nand_290_out, nand_291_out,
       nand_292_out, nand_293_out, nand_294_out, nand_295_out, nand_296_out, nand_297_out, nand_298_out,
       nand_299_out, nand_300_out, nand_301_out, nand_302_out, nand_303_out, nand_304_out, nand_305_out,
       nand_306_out, nand_307_out, nand_308_out, nand_309_out, nand_310_out, nand_311_out, nand_313_out,
       nand_314_out, nand_315_out, nand_316_out, nand_317_out, nand_318_out;

  nand nand_1 (nand_1_out, t_in[5], t_in[5]);
  nand nand_2 (nand_2_out, t_in[4], t_in[4]);
  nand nand_3 (nand_3_out, t_in[5], t_in[5]);
  nand nand_4 (nand_4_out, t_in[4], t_in[4]);
  nand nand_5 (nand_5_out, t_in[4], t_in[4]);
  nand nand_6 (nand_6_out, t_in[5], t_in[5]);
  nand nand_7 (nand_7_out, t_in[4], t_in[4]);
  nand nand_8 (nand_8_out, t_in[3], t_in[3]);
  nand nand_9 (nand_9_out, t_in[5], t_in[5]);
  nand nand_10 (nand_10_out, t_in[3], t_in[3]);
  nand nand_11 (nand_11_out, t_in[5], t_in[5]);
  nand nand_12 (nand_12_out, t_in[4], t_in[4]);
  nand nand_13 (nand_13_out, t_in[5], t_in[5]);
  nand nand_14 (nand_14_out, t_in[5], t_in[5]);
  nand nand_15 (nand_15_out, t_in[4], t_in[4]);
  nand nand_16 (nand_16_out, t_in[3], t_in[3]);
  nand nand_17 (nand_17_out, t_in[1], t_in[1]);
  nand nand_18 (nand_18_out, t_in[3], t_in[3]);
  nand nand_19 (nand_19_out, t_in[1], t_in[1]);
  nand nand_20 (nand_20_out, t_in[5], t_in[3]);
  nand nand_21 (nand_21_out, t_in[5], t_in[4]);
  nand nand_22 (nand_22_out, t_in[5], t_in[5]);
  nand nand_23 (nand_23_out, t_in[5], t_in[5]);
  nand nand_24 (nand_24_out, t_in[4], t_in[4]);
  nand nand_25 (nand_25_out, t_in[5], t_in[5]);
  nand nand_26 (nand_26_out, t_in[4], t_in[4]);
  nand nand_27 (nand_27_out, t_in[5], t_in[5]);
  nand nand_28 (nand_28_out, t_in[4], t_in[4]);
  nand nand_29 (nand_29_out, t_in[5], t_in[5]);
  nand nand_30 (nand_30_out, t_in[5], t_in[5]);
  nand nand_31 (nand_31_out, t_in[3], t_in[3]);
  nand nand_32 (nand_32_out, t_in[2], t_in[2]);
  nand nand_33 (nand_33_out, t_in[4], t_in[4]);
  nand nand_34 (nand_34_out, t_in[3], t_in[3]);
  nand nand_35 (nand_35_out, t_in[3], t_in[3]);
  nand nand_36 (nand_36_out, t_in[2], t_in[2]);
  nand nand_37 (nand_37_out, nand_1_out, nand_2_out);
  nand nand_38 (nand_38_out, nand_3_out, t_in[4]);
  nand nand_39 (nand_39_out, t_in[5], nand_4_out);
  nand nand_40 (nand_40_out, t_in[5], t_in[4]);
  nand nand_41 (nand_41_out, t_in[5], nand_5_out);
  nand nand_42 (nand_42_out, t_in[5], t_in[4]);
  nand nand_43 (nand_43_out, nand_6_out, nand_7_out);
  nand nand_44 (nand_44_out, nand_8_out, t_in[1]);
  nand nand_45 (nand_45_out, nand_9_out, nand_10_out);
  nand nand_46 (nand_46_out, t_in[2], t_in[1]);
  nand nand_47 (nand_47_out, nand_11_out, nand_12_out);
  nand nand_48 (nand_48_out, nand_13_out, t_in[4]);
  nand nand_49 (nand_49_out, nand_14_out, t_in[4]);
  nand nand_50 (nand_50_out, t_in[5], nand_15_out);
  nand nand_51 (nand_51_out, nand_16_out, nand_17_out);
  nand nand_52 (nand_52_out, t_in[5], nand_18_out);
  nand nand_53 (nand_53_out, t_in[2], nand_19_out);
  nand nand_54 (nand_54_out, t_in[5], t_in[4]);
  nand nand_55 (O_1[2], nand_20_out, nand_21_out);
  nand nand_56 (nand_56_out, nand_22_out, t_in[4]);
  nand nand_57 (nand_57_out, nand_23_out, t_in[4]);
  nand nand_58 (nand_58_out, t_in[4], t_in[3]);
  nand nand_59 (nand_59_out, t_in[5], nand_24_out);
  nand nand_60 (nand_60_out, nand_25_out, nand_26_out);
  nand nand_61 (nand_61_out, t_in[3], t_in[1]);
  nand nand_62 (nand_62_out, nand_27_out, nand_28_out);
  nand nand_63 (nand_63_out, t_in[3], t_in[2]);
  nand nand_64 (nand_64_out, nand_29_out, t_in[3]);
  nand nand_65 (nand_65_out, t_in[2], t_in[1]);
  nand nand_66 (nand_66_out, nand_30_out, t_in[4]);
  nand nand_67 (nand_67_out, nand_31_out, nand_32_out);
  nand nand_68 (nand_68_out, t_in[5], nand_33_out);
  nand nand_69 (nand_69_out, t_in[5], nand_34_out);
  nand nand_70 (nand_70_out, t_in[5], nand_35_out);
  nand nand_71 (nand_71_out, t_in[5], t_in[4]);
  nand nand_72 (nand_72_out, t_in[3], nand_36_out);
  nand nand_73 (nand_73_out, nand_37_out, nand_37_out);
  nand nand_74 (nand_74_out, t_in[2], t_in[2]);
  nand nand_75 (nand_75_out, t_in[1], t_in[1]);
  nand nand_76 (nand_76_out, nand_38_out, nand_38_out);
  nand nand_77 (nand_77_out, t_in[3], t_in[3]);
  nand nand_78 (nand_78_out, t_in[2], t_in[2]);
  nand nand_79 (nand_79_out, t_in[5], t_in[5]);
  nand nand_80 (nand_80_out, nand_39_out, nand_39_out);
  nand nand_81 (nand_81_out, t_in[3], t_in[3]);
  nand nand_82 (nand_82_out, nand_40_out, nand_40_out);
  nand nand_83 (nand_83_out, t_in[3], t_in[3]);
  nand nand_84 (nand_84_out, t_in[2], t_in[2]);
  nand nand_85 (nand_85_out, t_in[1], t_in[1]);
  nand nand_86 (nand_86_out, t_in[4], t_in[4]);
  nand nand_87 (nand_87_out, t_in[3], t_in[3]);
  nand nand_88 (nand_88_out, t_in[1], t_in[1]);
  nand nand_89 (nand_89_out, t_in[5], t_in[5]);
  nand nand_90 (nand_90_out, t_in[4], t_in[4]);
  nand nand_91 (nand_91_out, t_in[5], t_in[5]);
  nand nand_92 (nand_92_out, t_in[2], t_in[2]);
  nand nand_93 (nand_93_out, t_in[1], t_in[1]);
  nand nand_94 (nand_94_out, t_in[5], t_in[5]);
  nand nand_95 (nand_95_out, t_in[2], t_in[2]);
  nand nand_96 (nand_96_out, t_in[2], t_in[2]);
  nand nand_97 (nand_97_out, t_in[1], t_in[1]);
  nand nand_98 (nand_98_out, nand_41_out, nand_41_out);
  nand nand_99 (nand_99_out, t_in[3], t_in[3]);
  nand nand_100 (nand_100_out, t_in[2], t_in[2]);
  nand nand_101 (nand_101_out, t_in[4], t_in[4]);
  nand nand_102 (nand_102_out, nand_42_out, nand_42_out);
  nand nand_103 (nand_103_out, t_in[3], t_in[3]);
  nand nand_104 (nand_104_out, nand_43_out, nand_43_out);
  nand nand_105 (nand_105_out, nand_44_out, nand_44_out);
  nand nand_106 (nand_106_out, nand_45_out, nand_45_out);
  nand nand_107 (nand_107_out, nand_46_out, nand_46_out);
  nand nand_108 (nand_108_out, nand_47_out, nand_47_out);
  nand nand_109 (nand_109_out, t_in[1], t_in[1]);
  nand nand_110 (nand_110_out, nand_48_out, nand_48_out);
  nand nand_111 (nand_111_out, t_in[3], t_in[3]);
  nand nand_112 (nand_112_out, t_in[2], t_in[2]);
  nand nand_113 (nand_113_out, t_in[1], t_in[1]);
  nand nand_114 (nand_114_out, nand_49_out, nand_49_out);
  nand nand_115 (nand_115_out, t_in[2], t_in[2]);
  nand nand_116 (nand_116_out, nand_50_out, nand_50_out);
  nand nand_117 (nand_117_out, nand_51_out, nand_51_out);
  nand nand_118 (nand_118_out, nand_52_out, nand_52_out);
  nand nand_119 (nand_119_out, nand_53_out, nand_53_out);
  nand nand_120 (nand_120_out, t_in[4], t_in[4]);
  nand nand_121 (nand_121_out, nand_54_out, nand_54_out);
  nand nand_122 (nand_122_out, t_in[2], t_in[2]);
  nand nand_123 (nand_123_out, t_in[1], t_in[1]);
  nand nand_124 (nand_124_out, nand_56_out, nand_56_out);
  nand nand_125 (nand_125_out, nand_57_out, nand_57_out);
  nand nand_126 (nand_126_out, nand_58_out, nand_58_out);
  nand nand_127 (nand_127_out, nand_59_out, nand_59_out);
  nand nand_128 (nand_128_out, t_in[3], t_in[3]);
  nand nand_129 (nand_129_out, nand_60_out, nand_60_out);
  nand nand_130 (nand_130_out, nand_61_out, nand_61_out);
  nand nand_131 (nand_131_out, nand_62_out, nand_62_out);
  nand nand_132 (nand_132_out, nand_63_out, nand_63_out);
  nand nand_133 (nand_133_out, nand_64_out, nand_64_out);
  nand nand_134 (nand_134_out, nand_65_out, nand_65_out);
  nand nand_135 (nand_135_out, nand_66_out, nand_66_out);
  nand nand_136 (nand_136_out, nand_67_out, nand_67_out);
  nand nand_137 (nand_137_out, nand_68_out, nand_68_out);
  nand nand_138 (nand_138_out, t_in[3], t_in[3]);
  nand nand_139 (nand_139_out, nand_69_out, nand_69_out);
  nand nand_140 (nand_140_out, nand_70_out, nand_70_out);
  nand nand_141 (nand_141_out, nand_71_out, nand_71_out);
  nand nand_142 (nand_142_out, nand_72_out, nand_72_out);
  nand nand_143 (nand_143_out, nand_73_out, t_in[3]);
  nand nand_144 (nand_144_out, nand_74_out, nand_75_out);
  nand nand_145 (nand_145_out, nand_76_out, nand_77_out);
  nand nand_146 (nand_146_out, nand_78_out, t_in[1]);
  nand nand_147 (nand_147_out, nand_79_out, t_in[4]);
  nand nand_148 (nand_148_out, nand_80_out, nand_81_out);
  nand nand_149 (nand_149_out, t_in[2], t_in[1]);
  nand nand_150 (nand_150_out, nand_82_out, nand_83_out);
  nand nand_151 (nand_151_out, nand_84_out, nand_85_out);
  nand nand_152 (nand_152_out, t_in[5], t_in[4]);
  nand nand_153 (nand_153_out, nand_86_out, nand_87_out);
  nand nand_154 (nand_154_out, t_in[2], nand_88_out);
  nand nand_155 (nand_155_out, nand_89_out, nand_90_out);
  nand nand_156 (nand_156_out, t_in[2], t_in[1]);
  nand nand_157 (nand_157_out, nand_91_out, t_in[4]);
  nand nand_158 (nand_158_out, nand_92_out, nand_93_out);
  nand nand_159 (nand_159_out, nand_94_out, t_in[4]);
  nand nand_160 (nand_160_out, t_in[3], nand_95_out);
  nand nand_161 (nand_161_out, t_in[4], t_in[3]);
  nand nand_162 (nand_162_out, nand_96_out, nand_97_out);
  nand nand_163 (nand_163_out, nand_98_out, nand_99_out);
  nand nand_164 (nand_164_out, nand_100_out, t_in[1]);
  nand nand_165 (nand_165_out, t_in[5], nand_101_out);
  nand nand_166 (nand_166_out, t_in[3], t_in[2]);
  nand nand_167 (nand_167_out, nand_102_out, nand_103_out);
  nand nand_168 (nand_168_out, t_in[2], t_in[1]);
  nand nand_169 (nand_169_out, nand_104_out, nand_105_out);
  nand nand_170 (nand_170_out, nand_106_out, nand_107_out);
  nand nand_171 (nand_171_out, nand_108_out, t_in[3]);
  nand nand_172 (nand_172_out, t_in[2], nand_109_out);
  nand nand_173 (nand_173_out, nand_110_out, nand_111_out);
  nand nand_174 (nand_174_out, nand_112_out, nand_113_out);
  nand nand_175 (nand_175_out, nand_114_out, t_in[3]);
  nand nand_176 (nand_176_out, nand_115_out, t_in[1]);
  nand nand_177 (nand_177_out, nand_116_out, nand_117_out);
  nand nand_178 (nand_178_out, nand_118_out, nand_119_out);
  nand nand_179 (nand_179_out, t_in[5], nand_120_out);
  nand nand_180 (nand_180_out, t_in[3], t_in[1]);
  nand nand_181 (nand_181_out, t_in[5], t_in[3]);
  nand nand_182 (nand_182_out, t_in[2], t_in[1]);
  nand nand_183 (nand_183_out, nand_121_out, t_in[3]);
  nand nand_184 (nand_184_out, nand_122_out, nand_123_out);
  nand nand_185 (nand_185_out, nand_124_out, t_in[2]);
  nand nand_186 (nand_186_out, nand_125_out, t_in[3]);
  nand nand_187 (nand_187_out, nand_126_out, t_in[2]);
  nand nand_188 (nand_188_out, nand_127_out, nand_128_out);
  nand nand_189 (nand_189_out, nand_129_out, nand_130_out);
  nand nand_190 (nand_190_out, nand_131_out, nand_132_out);
  nand nand_191 (nand_191_out, nand_133_out, nand_134_out);
  nand nand_192 (nand_192_out, nand_135_out, nand_136_out);
  nand nand_193 (nand_193_out, nand_137_out, nand_138_out);
  nand nand_194 (nand_194_out, nand_139_out, t_in[1]);
  nand nand_195 (nand_195_out, nand_140_out, t_in[2]);
  nand nand_196 (nand_196_out, nand_141_out, nand_142_out);
  nand nand_197 (nand_197_out, nand_143_out, nand_143_out);
  nand nand_198 (nand_198_out, nand_144_out, nand_144_out);
  nand nand_199 (nand_199_out, nand_145_out, nand_145_out);
  nand nand_200 (nand_200_out, nand_146_out, nand_146_out);
  nand nand_201 (nand_201_out, nand_147_out, nand_147_out);
  nand nand_202 (nand_202_out, t_in[1], t_in[1]);
  nand nand_203 (nand_203_out, nand_148_out, nand_148_out);
  nand nand_204 (nand_204_out, nand_149_out, nand_149_out);
  nand nand_205 (nand_205_out, nand_150_out, nand_150_out);
  nand nand_206 (nand_206_out, nand_151_out, nand_151_out);
  nand nand_207 (nand_207_out, nand_152_out, nand_152_out);
  nand nand_208 (nand_208_out, t_in[2], t_in[2]);
  nand nand_209 (nand_209_out, nand_153_out, nand_153_out);
  nand nand_210 (nand_210_out, nand_154_out, nand_154_out);
  nand nand_211 (nand_211_out, nand_155_out, nand_155_out);
  nand nand_212 (nand_212_out, nand_156_out, nand_156_out);
  nand nand_213 (nand_213_out, nand_157_out, nand_157_out);
  nand nand_214 (nand_214_out, nand_158_out, nand_158_out);
  nand nand_215 (nand_215_out, nand_159_out, nand_159_out);
  nand nand_216 (nand_216_out, nand_160_out, nand_160_out);
  nand nand_217 (nand_217_out, nand_161_out, nand_161_out);
  nand nand_218 (nand_218_out, nand_162_out, nand_162_out);
  nand nand_219 (nand_219_out, nand_163_out, nand_163_out);
  nand nand_220 (nand_220_out, nand_164_out, nand_164_out);
  nand nand_221 (nand_221_out, nand_165_out, nand_165_out);
  nand nand_222 (nand_222_out, nand_166_out, nand_166_out);
  nand nand_223 (nand_223_out, nand_167_out, nand_167_out);
  nand nand_224 (nand_224_out, nand_168_out, nand_168_out);
  nand nand_225 (nand_225_out, nand_169_out, nand_170_out);
  nand nand_226 (nand_226_out, nand_171_out, nand_171_out);
  nand nand_227 (nand_227_out, nand_172_out, nand_172_out);
  nand nand_228 (nand_228_out, nand_173_out, nand_173_out);
  nand nand_229 (nand_229_out, nand_174_out, nand_174_out);
  nand nand_230 (nand_230_out, nand_175_out, nand_175_out);
  nand nand_231 (nand_231_out, nand_176_out, nand_176_out);
  nand nand_232 (nand_232_out, nand_177_out, nand_178_out);
  nand nand_233 (nand_233_out, nand_179_out, nand_179_out);
  nand nand_234 (nand_234_out, nand_180_out, nand_180_out);
  nand nand_235 (nand_235_out, nand_181_out, nand_181_out);
  nand nand_236 (nand_236_out, nand_182_out, nand_182_out);
  nand nand_237 (nand_237_out, nand_183_out, nand_183_out);
  nand nand_238 (nand_238_out, nand_184_out, nand_184_out);
  nand nand_239 (nand_239_out, nand_185_out, nand_186_out);
  nand nand_240 (nand_240_out, nand_187_out, nand_188_out);
  nand nand_241 (nand_241_out, nand_189_out, nand_190_out);
  nand nand_242 (nand_242_out, nand_191_out, nand_192_out);
  nand nand_243 (nand_243_out, nand_193_out, nand_194_out);
  nand nand_244 (nand_244_out, nand_195_out, nand_196_out);
  nand nand_245 (nand_245_out, nand_197_out, nand_198_out);
  nand nand_246 (nand_246_out, nand_199_out, nand_200_out);
  nand nand_247 (nand_247_out, nand_201_out, t_in[3]);
  nand nand_248 (nand_248_out, t_in[2], nand_202_out);
  nand nand_249 (nand_249_out, nand_203_out, nand_204_out);
  nand nand_250 (nand_250_out, nand_205_out, nand_206_out);
  nand nand_251 (nand_251_out, nand_207_out, t_in[3]);
  nand nand_252 (nand_252_out, nand_208_out, t_in[1]);
  nand nand_253 (nand_253_out, nand_209_out, nand_210_out);
  nand nand_254 (nand_254_out, nand_211_out, nand_212_out);
  nand nand_255 (nand_255_out, nand_213_out, nand_214_out);
  nand nand_256 (nand_256_out, nand_215_out, nand_216_out);
  nand nand_257 (nand_257_out, nand_217_out, nand_218_out);
  nand nand_258 (nand_258_out, nand_219_out, nand_220_out);
  nand nand_259 (nand_259_out, nand_221_out, nand_222_out);
  nand nand_260 (nand_260_out, nand_223_out, nand_224_out);
  nand nand_261 (nand_261_out, nand_225_out, nand_225_out);
  nand nand_262 (nand_262_out, nand_226_out, nand_227_out);
  nand nand_263 (nand_263_out, nand_228_out, nand_229_out);
  nand nand_264 (nand_264_out, nand_230_out, nand_231_out);
  nand nand_265 (nand_265_out, nand_232_out, nand_232_out);
  nand nand_266 (nand_266_out, nand_233_out, nand_234_out);
  nand nand_267 (nand_267_out, nand_235_out, nand_236_out);
  nand nand_268 (nand_268_out, nand_237_out, nand_238_out);
  nand nand_269 (nand_269_out, nand_239_out, nand_239_out);
  nand nand_270 (nand_270_out, nand_240_out, nand_240_out);
  nand nand_271 (nand_271_out, nand_241_out, nand_241_out);
  nand nand_272 (nand_272_out, nand_242_out, nand_242_out);
  nand nand_273 (nand_273_out, nand_243_out, nand_243_out);
  nand nand_274 (nand_274_out, nand_244_out, nand_244_out);
  nand nand_275 (nand_275_out, nand_245_out, nand_246_out);
  nand nand_276 (nand_276_out, nand_247_out, nand_247_out);
  nand nand_277 (nand_277_out, nand_248_out, nand_248_out);
  nand nand_278 (nand_278_out, nand_249_out, nand_250_out);
  nand nand_279 (nand_279_out, nand_251_out, nand_251_out);
  nand nand_280 (nand_280_out, nand_252_out, nand_252_out);
  nand nand_281 (nand_281_out, nand_253_out, nand_254_out);
  nand nand_282 (nand_282_out, nand_255_out, nand_256_out);
  nand nand_283 (nand_283_out, nand_257_out, nand_258_out);
  nand nand_284 (nand_284_out, nand_259_out, nand_260_out);
  nand nand_285 (nand_285_out, nand_261_out, nand_262_out);
  nand nand_286 (nand_286_out, nand_263_out, nand_264_out);
  nand nand_287 (nand_287_out, nand_265_out, nand_266_out);
  nand nand_288 (nand_288_out, nand_267_out, nand_268_out);
  nand nand_289 (O_1[1], nand_269_out, nand_270_out);
  nand nand_290 (nand_290_out, nand_271_out, nand_272_out);
  nand nand_291 (nand_291_out, nand_273_out, nand_274_out);
  nand nand_292 (nand_292_out, nand_275_out, nand_275_out);
  nand nand_293 (nand_293_out, nand_276_out, nand_277_out);
  nand nand_294 (nand_294_out, nand_278_out, nand_278_out);
  nand nand_295 (nand_295_out, nand_279_out, nand_280_out);
  nand nand_296 (nand_296_out, nand_281_out, nand_281_out);
  nand nand_297 (nand_297_out, nand_282_out, nand_282_out);
  nand nand_298 (nand_298_out, nand_283_out, nand_283_out);
  nand nand_299 (nand_299_out, nand_284_out, nand_284_out);
  nand nand_300 (nand_300_out, nand_285_out, nand_285_out);
  nand nand_301 (nand_301_out, nand_286_out, nand_286_out);
  nand nand_302 (nand_302_out, nand_287_out, nand_287_out);
  nand nand_303 (nand_303_out, nand_288_out, nand_288_out);
  nand nand_304 (nand_304_out, nand_290_out, nand_290_out);
  nand nand_305 (nand_305_out, nand_291_out, nand_291_out);
  nand nand_306 (nand_306_out, nand_292_out, nand_293_out);
  nand nand_307 (nand_307_out, nand_294_out, nand_295_out);
  nand nand_308 (nand_308_out, nand_296_out, nand_297_out);
  nand nand_309 (nand_309_out, nand_298_out, nand_299_out);
  nand nand_310 (nand_310_out, nand_300_out, nand_301_out);
  nand nand_311 (nand_311_out, nand_302_out, nand_303_out);
  nand nand_312 (O_1[0], nand_304_out, nand_305_out);
  nand nand_313 (nand_313_out, nand_306_out, nand_306_out);
  nand nand_314 (nand_314_out, nand_307_out, nand_307_out);
  nand nand_315 (nand_315_out, nand_308_out, nand_308_out);
  nand nand_316 (nand_316_out, nand_309_out, nand_309_out);
  nand nand_317 (nand_317_out, nand_310_out, nand_310_out);
  nand nand_318 (nand_318_out, nand_311_out, nand_311_out);
  nand nand_319 (O_0[3], nand_313_out, nand_314_out);
  nand nand_320 (O_0[2], nand_315_out, nand_316_out);
  nand nand_321 (O_0[1], nand_317_out, nand_318_out);

  assign {O_0[4], O_0[0]} = {1'b0, t_in[0]};
  assign O_1[4:3] = 2'b00;
endmodule

module test (
  input  C_2,
  input  C_1,
  input  C_0,
  input  S_3,
  input  S_2,
  input  S_1,
  input  S_0,
  output O_3,
  output O_2,
  output O_1,
  output O_0
);

  wire and_1_out, and_2_out, and_3_out, and_4_out, and_5_out, and_6_out, and_7_out, and_8_out, and_9_out,
       and_10_out, and_11_out, and_12_out, and_13_out, and_14_out, and_15_out, and_16_out, and_17_out,
       and_18_out, and_19_out, and_20_out, and_21_out, and_22_out, and_23_out, and_24_out, and_25_out,
       and_26_out, and_27_out, and_28_out, and_29_out, and_30_out, and_31_out, and_32_out, and_33_out,
       and_34_out, and_35_out, and_36_out, and_37_out, not_1_out, not_2_out, not_3_out, not_4_out, not_5_out,
       not_6_out, not_7_out, not_8_out, not_9_out, not_10_out, not_11_out, not_12_out, not_13_out,
       not_14_out, not_15_out, not_16_out, not_17_out, not_18_out, not_19_out, not_20_out, not_21_out,
       not_22_out, not_23_out, not_24_out, not_25_out, not_26_out, not_27_out, not_28_out, not_29_out,
       not_30_out, not_31_out, not_32_out, not_33_out, not_34_out, not_35_out, not_36_out, not_37_out,
       not_38_out, not_39_out, not_40_out, not_41_out, not_42_out, not_43_out, not_44_out, not_45_out,
       not_46_out, not_47_out, not_48_out, not_49_out, not_50_out, not_51_out, not_52_out, not_53_out,
       not_54_out, not_55_out, not_56_out, not_57_out, not_58_out, not_59_out, not_60_out, not_61_out,
       not_62_out, not_63_out, not_64_out, not_65_out, not_66_out, not_67_out, not_68_out, not_69_out,
       not_70_out, not_71_out, not_72_out, not_73_out, not_74_out, not_75_out, not_76_out, not_77_out,
       not_78_out, not_79_out, not_80_out, not_81_out, not_82_out, not_83_out, not_84_out, not_85_out,
       not_86_out, not_87_out, not_88_out, not_89_out, not_90_out, not_91_out, not_92_out, not_93_out,
       not_94_out;

  not not_1 (not_1_out, C_2);
  not not_2 (not_2_out, C_1);
  not not_3 (not_3_out, C_0);
  not not_4 (not_4_out, S_2);
  not not_5 (not_5_out, C_1);
  not not_6 (not_6_out, C_0);
  not not_7 (not_7_out, C_1);
  not not_8 (not_8_out, S_3);
  not not_9 (not_9_out, C_2);
  not not_10 (not_10_out, C_1);
  not not_11 (not_11_out, S_3);
  not not_12 (not_12_out, S_1);
  not not_13 (not_13_out, C_1);
  not not_14 (not_14_out, S_3);
  not not_15 (not_15_out, S_0);
  not not_16 (not_16_out, C_1);
  not not_17 (not_17_out, C_0);
  not not_18 (not_18_out, C_2);
  not not_19 (not_19_out, C_0);
  not not_20 (not_20_out, C_1);
  not not_21 (not_21_out, C_0);
  not not_22 (not_22_out, C_2);
  not not_23 (not_23_out, C_1);
  not not_24 (not_24_out, C_2);
  not not_25 (not_25_out, S_0);
  not not_26 (not_26_out, C_1);
  not not_27 (not_27_out, C_0);
  not not_28 (not_28_out, S_0);
  not not_29 (not_29_out, C_1);
  not not_30 (not_30_out, S_3);
  not not_31 (not_31_out, S_2);
  not not_32 (not_32_out, C_1);
  not not_33 (not_33_out, S_3);
  not not_34 (not_34_out, S_0);
  not not_35 (not_35_out, C_2);
  not not_36 (not_36_out, C_1);
  not not_37 (not_37_out, C_0);
  not not_38 (not_38_out, C_2);
  not not_39 (not_39_out, C_2);
  not not_40 (not_40_out, C_1);
  not not_41 (not_41_out, S_2);
  not not_42 (not_42_out, C_2);
  not not_43 (not_43_out, C_0);
  not not_44 (not_44_out, S_3);
  not not_45 (not_45_out, C_2);
  not not_46 (not_46_out, S_3);
  not not_47 (not_47_out, S_2);
  not not_48 (not_48_out, C_2);
  not not_49 (not_49_out, C_1);
  not not_50 (not_50_out, C_0);
  not not_51 (not_51_out, C_2);
  not not_52 (not_52_out, C_0);
  not not_53 (not_53_out, S_2);
  not not_54 (not_54_out, S_1);
  not not_55 (not_55_out, C_1);
  not not_56 (not_56_out, C_0);
  not not_57 (not_57_out, S_2);
  not not_58 (not_58_out, S_1);
  not not_59 (not_59_out, C_1);
  not not_60 (not_60_out, S_3);
  not not_61 (not_61_out, S_2);
  not not_62 (not_62_out, C_1);
  not not_63 (not_63_out, S_3);
  not not_64 (not_64_out, S_1);
  not not_65 (not_65_out, C_2);
  not not_66 (not_66_out, C_1);
  not not_67 (not_67_out, C_0);
  not not_68 (not_68_out, C_2);
  not not_69 (not_69_out, C_1);
  not not_70 (not_70_out, S_3);
  not not_71 (not_71_out, S_2);
  not not_72 (not_72_out, C_2);
  not not_73 (not_73_out, C_2);
  not not_74 (not_74_out, C_2);
  not not_75 (not_75_out, C_0);
  not not_76 (not_76_out, S_3);
  not not_77 (not_77_out, S_2);
  not not_78 (not_78_out, S_1);
  not not_79 (not_79_out, C_2);
  not not_80 (not_80_out, C_0);
  not not_81 (not_81_out, S_2);
  not not_82 (not_82_out, C_2);
  not not_83 (not_83_out, C_0);
  not not_84 (not_84_out, S_1);
  not not_85 (not_85_out, C_2);
  not not_86 (not_86_out, S_2);
  not not_87 (not_87_out, S_1);
  not not_88 (not_88_out, C_1);
  not not_89 (not_89_out, C_0);
  not not_90 (not_90_out, S_3);
  not not_91 (not_91_out, S_1);
  not not_92 (not_92_out, C_1);
  not not_93 (not_93_out, S_3);
  not not_94 (not_94_out, S_0);
  and and_1 (and_1_out, not_1_out, S_3);
  and and_2 (and_2_out, not_2_out, not_3_out, S_3, not_4_out);
  and and_3 (and_3_out, not_5_out, not_6_out, S_3, S_1);
  and and_4 (and_4_out, C_2, not_7_out, C_0, not_8_out, S_2, S_1, S_0);
  and and_5 (and_5_out, not_9_out, S_2);
  and and_6 (and_6_out, not_10_out, not_11_out, S_2, not_12_out);
  and and_7 (and_7_out, not_13_out, not_14_out, S_2, not_15_out);
  and and_8 (and_8_out, not_16_out, not_17_out, S_2, S_1);
  and and_9 (and_9_out, not_18_out, C_1, not_19_out, S_1, S_0);
  and and_10 (and_10_out, C_2, not_20_out, not_21_out, S_3, S_1, S_0);
  and and_11 (and_11_out, not_22_out, not_23_out, S_1);
  and and_12 (and_12_out, not_24_out, S_1, not_25_out);
  and and_13 (and_13_out, not_26_out, not_27_out, S_1, not_28_out);
  and and_14 (and_14_out, not_29_out, not_30_out, not_31_out, S_1);
  and and_15 (and_15_out, not_32_out, not_33_out, S_1, not_34_out);
  and and_16 (and_16_out, not_35_out, S_2, S_1);
  and and_17 (and_17_out, not_36_out, not_37_out, S_2, S_1);
  and and_18 (and_18_out, not_38_out, C_0, S_1);
  and and_19 (and_19_out, not_39_out, not_40_out, C_0, S_3, not_41_out, S_0);
  and and_20 (and_20_out, not_42_out, C_1, not_43_out, not_44_out, S_2);
  and and_21 (and_21_out, not_45_out, C_1, C_0, not_46_out, not_47_out, S_0);
  and and_22 (and_22_out, not_48_out, not_49_out, not_50_out, S_0);
  and and_23 (and_23_out, not_51_out, not_52_out, not_53_out, not_54_out, S_0);
  and and_24 (and_24_out, not_55_out, not_56_out, not_57_out, not_58_out, S_0);
  and and_25 (and_25_out, not_59_out, not_60_out, not_61_out, S_0);
  and and_26 (and_26_out, not_62_out, not_63_out, not_64_out, S_0);
  and and_27 (and_27_out, not_65_out, S_2, S_1, S_0);
  and and_28 (and_28_out, not_66_out, not_67_out, S_2, S_1, S_0);
  and and_29 (and_29_out, not_68_out, not_69_out, C_0, not_70_out, not_71_out, S_1);
  and and_30 (and_30_out, not_72_out, C_0, S_1, S_0);
  and and_31 (and_31_out, not_73_out, C_0, S_2, S_0);
  and and_32 (and_32_out, not_74_out, C_1, not_75_out, not_76_out, not_77_out, not_78_out);
  and and_33 (and_33_out, not_79_out, C_1, not_80_out, S_3, not_81_out, S_1);
  and and_34 (and_34_out, not_82_out, C_1, not_83_out, S_3, S_2, not_84_out);
  and and_35 (and_35_out, not_85_out, C_1, C_0, S_3, not_86_out, not_87_out);
  and and_36 (and_36_out, C_2, not_88_out, not_89_out, not_90_out, S_2, not_91_out);
  and and_37 (and_37_out, C_2, not_92_out, C_0, not_93_out, S_2, S_1, not_94_out);
  or or_1 (O_3, and_1_out, and_2_out, and_3_out, and_4_out);
  or or_2 (O_2, and_5_out, and_6_out, and_7_out, and_8_out, and_9_out, and_10_out);
  or or_3 (O_1, and_11_out, and_12_out, and_13_out, and_14_out, and_15_out, and_16_out, and_17_out, and_18_out, and_19_out, and_20_out, and_21_out);
  or or_4 (O_0, and_22_out, and_23_out, and_24_out, and_25_out, and_26_out, and_27_out, and_28_out, and_29_out, and_30_out, and_31_out, and_32_out, and_33_out, and_34_out, and_35_out, and_36_out, and_37_out);
endmodule

module memory_alarm (
  input  [5:0] hour_in,
  input  [5:0] min_in,
  input  [5:0] sec_in,
  input  set,
  input  reset,
  input  enable,
  output [5:0] hour,
  output [5:0] min,
  output [5:0] seconds
);

  Register #(.width(6)) register_1 (.D(hour_in), .en(enable), .clk(set), .Q(hour), .clr(reset));
  Register #(.width(6)) register_2 (.D(min_in), .en(enable), .clk(set), .Q(min), .clr(reset));
  Register #(.width(6)) register_3 (.D(sec_in), .en(enable), .clk(set), .Q(seconds), .clr(reset));
endmodule

module music_givenTheme (
  input  Ds,
  input  E,
  input  F,
  input  Fs,
  input  G,
  input  B,
  input  A2,
  input  B2,
  input  reset,
  input  music_clock,
  input  in_11,
  output freq
);

  wire clock_1_out, clock_2_out, music_givenTheme_logic_1_o_0, music_givenTheme_logic_1_o_1,
       music_givenTheme_logic_1_o_2, music_givenTheme_logic_1_o_3, not_1_out, not_2_out, not_3_out,
       not_4_out, or_1_out, shift_register_1_p2, shift_register_1_p3;
  wire [2:0] counter_1_q;
  wire [3:0] s_r_ff_4_q;

  Clock #(.highDuration(20), .lowDuration(20)) clock_1 (.out(clock_1_out));
  Clock clock_2 (.out(clock_2_out));
  Counter #(.width(3), .max('h7)) counter_1 (
    .clr(or_1_out), .load(1'b0), .up(1'b1), .count(1'b1), .clk(clock_1_out), .D(3'b000), .Q(counter_1_q));  // open: carry
  or or_1 (or_1_out, reset, shift_register_1_p3);
  Multiplexer #(.select(4), .enable("false")) multiplexer_1 (
    .in0(B), .in1(E), .in2(G), .in3(F), .in4(E), .in5(B2), .in6(A2), .in7(Fs), .in8(E), .in9(G), .in10(F),
    .in11(Ds), .in12(F), .in13(B), .out(freq), .sel(s_r_ff_4_q));  // open: in14, in15
  // Probe on s_r_ff_4_q
  // Shift_Register #(.length(1)) shift_register_1: pin names not known; wires that end beside it: clock_2_out, shift_register_1_p2, shift_register_1_p3
  music_givenTheme_logic music_givenTheme_logic_1 (
    .C_2(counter_1_q[2]), .C_1(counter_1_q[1]), .C_0(counter_1_q[0]), .S_3(s_r_ff_4_q[3]),
    .S_2(s_r_ff_4_q[2]), .S_1(s_r_ff_4_q[1]), .S_0(s_r_ff_4_q[0]), .O_3(music_givenTheme_logic_1_o_3),
    .O_2(music_givenTheme_logic_1_o_2), .O_1(music_givenTheme_logic_1_o_1),
    .O_0(music_givenTheme_logic_1_o_0), .reset(shift_register_1_p2));
  S_R_Flip_Flop s_r_ff_1 (
    .S(music_givenTheme_logic_1_o_3), .R(not_1_out), .clk(clock_2_out), .Q(s_r_ff_4_q[3]), .reset(reset));  // open: Qn, preset
  not not_1 (not_1_out, music_givenTheme_logic_1_o_3);
  S_R_Flip_Flop s_r_ff_2 (
    .S(music_givenTheme_logic_1_o_2), .R(not_2_out), .clk(clock_2_out), .Q(s_r_ff_4_q[2]), .reset(reset));  // open: Qn, preset
  not not_2 (not_2_out, music_givenTheme_logic_1_o_2);
  S_R_Flip_Flop s_r_ff_3 (
    .S(music_givenTheme_logic_1_o_1), .R(not_3_out), .clk(clock_2_out), .Q(s_r_ff_4_q[1]), .reset(reset));  // open: Qn, preset
  not not_3 (not_3_out, music_givenTheme_logic_1_o_1);
  S_R_Flip_Flop s_r_ff_4 (
    .S(music_givenTheme_logic_1_o_0), .R(not_4_out), .clk(clock_2_out), .Q(s_r_ff_4_q[0]), .reset(reset));  // open: Qn, preset
  not not_4 (not_4_out, music_givenTheme_logic_1_o_0);
endmodule
module music_givenTheme_logic (
  input  C_2,
  input  C_1,
  input  C_0,
  input  S_3,
  input  S_2,
  input  S_1,
  input  S_0,
  output O_3,
  output O_2,
  output O_1,
  output O_0,
  output reset
);

  wire and_1_out, and_2_out, and_3_out, and_4_out, and_5_out, and_6_out, and_7_out, and_8_out, and_9_out,
       and_10_out, and_11_out, and_12_out, and_13_out, and_14_out, and_15_out, and_16_out, and_17_out,
       and_18_out, and_19_out, and_20_out, and_21_out, and_22_out, and_23_out, and_24_out, and_25_out,
       and_26_out, and_27_out, and_28_out, and_29_out, and_30_out, and_31_out, and_32_out, and_33_out,
       and_34_out, and_35_out, and_36_out, and_37_out, and_38_out, and_39_out, and_40_out, and_41_out,
       and_42_out, and_43_out, and_44_out, and_45_out, and_46_out, and_47_out, and_48_out, and_49_out,
       and_50_out, not_1_out, not_2_out, not_3_out, not_4_out, not_5_out, not_6_out, not_7_out, not_8_out,
       not_9_out, not_10_out, not_11_out, not_12_out, not_13_out, not_14_out, not_15_out, not_16_out,
       not_17_out, not_18_out, not_19_out, not_20_out, not_21_out, not_22_out, not_23_out, not_24_out,
       not_25_out, not_26_out, not_27_out, not_28_out, not_29_out, not_30_out, not_31_out, not_32_out,
       not_33_out, not_34_out, not_35_out, not_36_out, not_37_out, not_38_out, not_39_out, not_40_out,
       not_41_out, not_42_out, not_43_out, not_44_out, not_45_out, not_46_out, not_47_out, not_48_out,
       not_49_out, not_50_out, not_51_out, not_52_out, not_53_out, not_54_out, not_55_out, not_56_out,
       not_57_out, not_58_out, not_59_out, not_60_out, not_61_out, not_62_out, not_63_out, not_64_out,
       not_65_out, not_66_out, not_67_out, not_68_out, not_69_out, not_70_out, not_71_out, not_72_out,
       not_73_out, not_74_out, not_75_out, not_76_out, not_77_out, not_78_out, not_79_out, not_80_out,
       not_81_out, not_82_out, not_83_out, not_84_out, not_85_out, not_86_out, not_87_out, not_88_out,
       not_89_out, not_90_out, not_91_out, not_92_out, not_93_out, not_94_out, not_95_out, not_96_out,
       not_97_out, not_98_out, not_99_out, not_100_out, not_101_out, not_102_out, not_103_out, not_104_out,
       not_105_out, not_106_out, not_107_out, not_108_out, not_109_out, not_110_out, not_111_out,
       not_112_out, not_113_out, not_114_out, not_115_out, not_116_out, not_117_out, not_118_out,
       not_119_out, not_120_out, not_121_out, not_122_out, not_123_out, not_124_out, not_125_out,
       not_126_out, not_127_out, not_128_out, not_129_out, not_130_out, not_131_out, not_132_out,
       not_133_out, not_134_out, not_135_out, not_136_out, not_137_out, not_138_out, not_139_out,
       not_140_out, not_141_out, not_142_out, not_143_out, not_144_out, not_145_out, not_146_out, not_147_out;

  not not_1 (not_1_out, C_2);
  not not_2 (not_2_out, C_1);
  not not_3 (not_3_out, C_0);
  not not_4 (not_4_out, S_2);
  not not_5 (not_5_out, C_1);
  not not_6 (not_6_out, C_0);
  not not_7 (not_7_out, S_0);
  not not_8 (not_8_out, C_1);
  not not_9 (not_9_out, C_0);
  not not_10 (not_10_out, C_1);
  not not_11 (not_11_out, S_3);
  not not_12 (not_12_out, C_2);
  not not_13 (not_13_out, C_1);
  not not_14 (not_14_out, C_0);
  not not_15 (not_15_out, S_3);
  not not_16 (not_16_out, C_1);
  not not_17 (not_17_out, C_0);
  not not_18 (not_18_out, S_0);
  not not_19 (not_19_out, C_1);
  not not_20 (not_20_out, S_3);
  not not_21 (not_21_out, S_1);
  not not_22 (not_22_out, C_1);
  not not_23 (not_23_out, S_3);
  not not_24 (not_24_out, S_0);
  not not_25 (not_25_out, C_2);
  not not_26 (not_26_out, C_0);
  not not_27 (not_27_out, S_3);
  not not_28 (not_28_out, C_1);
  not not_29 (not_29_out, C_0);
  not not_30 (not_30_out, C_2);
  not not_31 (not_31_out, S_0);
  not not_32 (not_32_out, C_1);
  not not_33 (not_33_out, C_0);
  not not_34 (not_34_out, S_0);
  not not_35 (not_35_out, C_1);
  not not_36 (not_36_out, S_3);
  not not_37 (not_37_out, S_2);
  not not_38 (not_38_out, C_1);
  not not_39 (not_39_out, S_3);
  not not_40 (not_40_out, S_0);
  not not_41 (not_41_out, C_1);
  not not_42 (not_42_out, C_0);
  not not_43 (not_43_out, C_2);
  not not_44 (not_44_out, C_2);
  not not_45 (not_45_out, C_2);
  not not_46 (not_46_out, C_1);
  not not_47 (not_47_out, S_2);
  not not_48 (not_48_out, C_2);
  not not_49 (not_49_out, C_0);
  not not_50 (not_50_out, S_3);
  not not_51 (not_51_out, C_2);
  not not_52 (not_52_out, S_3);
  not not_53 (not_53_out, S_2);
  not not_54 (not_54_out, C_1);
  not not_55 (not_55_out, C_0);
  not not_56 (not_56_out, S_2);
  not not_57 (not_57_out, S_1);
  not not_58 (not_58_out, C_1);
  not not_59 (not_59_out, S_3);
  not not_60 (not_60_out, S_2);
  not not_61 (not_61_out, C_1);
  not not_62 (not_62_out, S_3);
  not not_63 (not_63_out, S_1);
  not not_64 (not_64_out, C_2);
  not not_65 (not_65_out, C_1);
  not not_66 (not_66_out, C_0);
  not not_67 (not_67_out, C_2);
  not not_68 (not_68_out, C_0);
  not not_69 (not_69_out, C_2);
  not not_70 (not_70_out, C_1);
  not not_71 (not_71_out, S_3);
  not not_72 (not_72_out, S_2);
  not not_73 (not_73_out, C_2);
  not not_74 (not_74_out, C_2);
  not not_75 (not_75_out, C_2);
  not not_76 (not_76_out, C_0);
  not not_77 (not_77_out, S_3);
  not not_78 (not_78_out, S_2);
  not not_79 (not_79_out, S_1);
  not not_80 (not_80_out, C_2);
  not not_81 (not_81_out, C_0);
  not not_82 (not_82_out, S_2);
  not not_83 (not_83_out, C_2);
  not not_84 (not_84_out, C_0);
  not not_85 (not_85_out, S_1);
  not not_86 (not_86_out, C_2);
  not not_87 (not_87_out, S_2);
  not not_88 (not_88_out, S_1);
  not not_89 (not_89_out, C_1);
  not not_90 (not_90_out, C_0);
  not not_91 (not_91_out, S_3);
  not not_92 (not_92_out, S_1);
  not not_93 (not_93_out, C_1);
  not not_94 (not_94_out, S_3);
  not not_95 (not_95_out, S_0);
  not not_96 (not_96_out, C_2);
  not not_97 (not_97_out, C_1);
  not not_98 (not_98_out, S_3);
  not not_99 (not_99_out, S_2);
  not not_100 (not_100_out, S_0);
  not not_101 (not_101_out, C_2);
  not not_102 (not_102_out, C_1);
  not not_103 (not_103_out, S_2);
  not not_104 (not_104_out, S_1);
  not not_105 (not_105_out, C_2);
  not not_106 (not_106_out, C_0);
  not not_107 (not_107_out, S_3);
  not not_108 (not_108_out, S_2);
  not not_109 (not_109_out, S_1);
  not not_110 (not_110_out, S_0);
  not not_111 (not_111_out, C_2);
  not not_112 (not_112_out, C_0);
  not not_113 (not_113_out, S_3);
  not not_114 (not_114_out, S_2);
  not not_115 (not_115_out, C_2);
  not not_116 (not_116_out, C_0);
  not not_117 (not_117_out, S_3);
  not not_118 (not_118_out, S_1);
  not not_119 (not_119_out, C_2);
  not not_120 (not_120_out, C_0);
  not not_121 (not_121_out, S_2);
  not not_122 (not_122_out, S_0);
  not not_123 (not_123_out, C_2);
  not not_124 (not_124_out, C_0);
  not not_125 (not_125_out, S_1);
  not not_126 (not_126_out, S_0);
  not not_127 (not_127_out, C_2);
  not not_128 (not_128_out, S_3);
  not not_129 (not_129_out, S_2);
  not not_130 (not_130_out, S_1);
  not not_131 (not_131_out, C_2);
  not not_132 (not_132_out, S_2);
  not not_133 (not_133_out, S_1);
  not not_134 (not_134_out, S_0);
  not not_135 (not_135_out, C_1);
  not not_136 (not_136_out, C_0);
  not not_137 (not_137_out, S_3);
  not not_138 (not_138_out, S_1);
  not not_139 (not_139_out, S_0);
  not not_140 (not_140_out, C_1);
  not not_141 (not_141_out, C_0);
  not not_142 (not_142_out, S_2);
  not not_143 (not_143_out, C_1);
  not not_144 (not_144_out, C_0);
  not not_145 (not_145_out, S_1);
  not not_146 (not_146_out, C_1);
  not not_147 (not_147_out, S_3);
  and and_1 (and_1_out, not_1_out, S_3);
  and and_2 (and_2_out, not_2_out, not_3_out, S_3, not_4_out);
  and and_3 (and_3_out, not_5_out, not_6_out, S_3, not_7_out);
  and and_4 (and_4_out, not_8_out, not_9_out, S_3, S_1);
  and and_5 (and_5_out, C_2, not_10_out, C_0, not_11_out, S_2, S_1, S_0);
  and and_6 (and_6_out, not_12_out, S_2);
  and and_7 (and_7_out, not_13_out, not_14_out, not_15_out, S_2);
  and and_8 (and_8_out, not_16_out, not_17_out, S_2, not_18_out);
  and and_9 (and_9_out, not_19_out, not_20_out, S_2, not_21_out);
  and and_10 (and_10_out, not_22_out, not_23_out, S_2, not_24_out);
  and and_11 (and_11_out, not_25_out, C_1, not_26_out, not_27_out, S_1, S_0);
  and and_12 (and_12_out, C_2, not_28_out, not_29_out, S_3, S_1, S_0);
  and and_13 (and_13_out, not_30_out, S_1, not_31_out);
  and and_14 (and_14_out, not_32_out, not_33_out, S_1, not_34_out);
  and and_15 (and_15_out, not_35_out, not_36_out, not_37_out, S_1);
  and and_16 (and_16_out, not_38_out, not_39_out, S_1, not_40_out);
  and and_17 (and_17_out, not_41_out, not_42_out, S_2, S_1);
  and and_18 (and_18_out, not_43_out, S_3, S_1);
  and and_19 (and_19_out, not_44_out, C_0, S_1);
  and and_20 (and_20_out, not_45_out, not_46_out, C_0, S_3, not_47_out, S_0);
  and and_21 (and_21_out, not_48_out, C_1, not_49_out, not_50_out, S_2, S_0);
  and and_22 (and_22_out, not_51_out, C_1, C_0, not_52_out, not_53_out, S_0);
  and and_23 (and_23_out, not_54_out, not_55_out, not_56_out, not_57_out, S_0);
  and and_24 (and_24_out, not_58_out, not_59_out, not_60_out, S_0);
  and and_25 (and_25_out, not_61_out, not_62_out, not_63_out, S_0);
  and and_26 (and_26_out, not_64_out, S_2, S_1, S_0);
  and and_27 (and_27_out, not_65_out, not_66_out, S_2, S_1, S_0);
  and and_28 (and_28_out, not_67_out, not_68_out, S_3, S_0);
  and and_29 (and_29_out, not_69_out, not_70_out, C_0, not_71_out, not_72_out, S_1);
  and and_30 (and_30_out, not_73_out, C_0, S_1, S_0);
  and and_31 (and_31_out, not_74_out, C_0, S_2, S_0);
  and and_32 (and_32_out, not_75_out, C_1, not_76_out, not_77_out, not_78_out, not_79_out);
  and and_33 (and_33_out, not_80_out, C_1, not_81_out, S_3, not_82_out, S_1);
  and and_34 (and_34_out, not_83_out, C_1, not_84_out, S_3, S_2, not_85_out);
  and and_35 (and_35_out, not_86_out, C_1, C_0, S_3, not_87_out, not_88_out);
  and and_36 (and_36_out, C_2, not_89_out, not_90_out, not_91_out, S_2, not_92_out);
  and and_37 (and_37_out, C_2, not_93_out, C_0, not_94_out, S_2, S_1, not_95_out);
  and and_38 (and_38_out, not_96_out, not_97_out, C_0, not_98_out, not_99_out, S_1, not_100_out);
  and and_39 (and_39_out, not_101_out, not_102_out, C_0, S_3, not_103_out, not_104_out, S_0);
  and and_40 (and_40_out, not_105_out, C_1, not_106_out, not_107_out, not_108_out, not_109_out, not_110_out);
  and and_41 (and_41_out, not_111_out, C_1, not_112_out, not_113_out, not_114_out, S_1, S_0);
  and and_42 (and_42_out, not_115_out, C_1, not_116_out, not_117_out, S_2, not_118_out, S_0);
  and and_43 (and_43_out, not_119_out, C_1, not_120_out, S_3, not_121_out, S_1, not_122_out);
  and and_44 (and_44_out, not_123_out, C_1, not_124_out, S_3, S_2, not_125_out, not_126_out);
  and and_45 (and_45_out, not_127_out, C_1, C_0, not_128_out, not_129_out, not_130_out, S_0);
  and and_46 (and_46_out, not_131_out, C_1, C_0, S_3, not_132_out, not_133_out, not_134_out);
  and and_47 (and_47_out, C_2, not_135_out, not_136_out, not_137_out, S_2, not_138_out, not_139_out);
  and and_48 (and_48_out, C_2, not_140_out, not_141_out, S_3, not_142_out, S_1, S_0);
  and and_49 (and_49_out, C_2, not_143_out, not_144_out, S_3, S_2, not_145_out, S_0);
  and and_50 (and_50_out, C_2, not_146_out, C_0, not_147_out, S_2, S_1);
  or or_1 (O_3, and_1_out, and_2_out, and_3_out, and_4_out, and_5_out);
  or or_2 (O_2, and_6_out, and_7_out, and_8_out, and_9_out, and_10_out, and_11_out, and_12_out);
  or or_3 (O_1, and_13_out, and_14_out, and_15_out, and_16_out, and_17_out, and_18_out, and_19_out, and_20_out, and_21_out, and_22_out);
  or or_4 (O_0, and_23_out, and_24_out, and_25_out, and_26_out, and_27_out, and_28_out, and_29_out, and_30_out, and_31_out, and_32_out, and_33_out, and_34_out, and_35_out, and_36_out, and_37_out);
  or or_5 (reset, and_38_out, and_39_out, and_40_out, and_41_out, and_42_out, and_43_out, and_44_out, and_45_out, and_46_out, and_47_out, and_48_out, and_49_out, and_50_out);
endmodule

module in_impeach (
  input  B_1,
  input  B_0,
  input  DS_9,
  input  DS_8,
  input  DS_7,
  input  DS_6,
  input  DS_5,
  input  DS_4,
  input  DS_3,
  input  DS_2,
  input  DS_1,
  input  DS_0,
  output O_1,
  output O_0
);

  wire nand_1_out, nand_2_out, nand_3_out, nand_4_out, nand_5_out, nand_6_out, nand_7_out, nand_8_out,
       nand_9_out, nand_10_out, nand_11_out, nand_12_out, nand_13_out, nand_14_out, nand_15_out, nand_16_out,
       nand_17_out, nand_18_out, nand_19_out, nand_20_out, nand_21_out, nand_22_out, nand_23_out,
       nand_24_out, nand_25_out, nand_26_out, nand_27_out, nand_28_out, nand_29_out, nand_30_out,
       nand_31_out, nand_32_out, nand_33_out, nand_34_out, nand_35_out, nand_36_out, nand_37_out,
       nand_38_out, nand_39_out, nand_40_out, nand_41_out, nand_42_out, nand_43_out, nand_44_out,
       nand_45_out, nand_46_out, nand_47_out, nand_48_out, nand_49_out, nand_50_out, nand_51_out,
       nand_52_out, nand_53_out, nand_54_out, nand_55_out, nand_56_out, nand_57_out, nand_58_out;

  nand nand_1 (nand_1_out, DS_0, DS_0);
  nand nand_2 (nand_2_out, DS_1, DS_1);
  nand nand_3 (nand_3_out, DS_3, DS_3);
  nand nand_4 (nand_4_out, DS_4, DS_4);
  nand nand_5 (nand_5_out, DS_6, DS_6);
  nand nand_6 (nand_6_out, DS_7, DS_7);
  nand nand_7 (nand_7_out, DS_0, DS_0);
  nand nand_8 (nand_8_out, DS_1, DS_1);
  nand nand_9 (nand_9_out, DS_3, DS_3);
  nand nand_10 (nand_10_out, DS_4, DS_4);
  nand nand_11 (nand_11_out, DS_6, DS_6);
  nand nand_12 (nand_12_out, DS_7, DS_7);
  nand nand_13 (nand_13_out, nand_1_out, nand_2_out);
  nand nand_14 (nand_14_out, nand_3_out, nand_4_out);
  nand nand_15 (nand_15_out, nand_5_out, nand_6_out);
  nand nand_16 (nand_16_out, nand_7_out, nand_8_out);
  nand nand_17 (nand_17_out, nand_9_out, nand_10_out);
  nand nand_18 (nand_18_out, nand_11_out, nand_12_out);
  nand nand_19 (nand_19_out, nand_13_out, nand_13_out);
  nand nand_20 (nand_20_out, DS_2, DS_2);
  nand nand_21 (nand_21_out, nand_14_out, nand_14_out);
  nand nand_22 (nand_22_out, DS_5, DS_5);
  nand nand_23 (nand_23_out, nand_15_out, nand_15_out);
  nand nand_24 (nand_24_out, DS_8, DS_8);
  nand nand_25 (nand_25_out, DS_9, DS_9);
  nand nand_26 (nand_26_out, nand_16_out, nand_16_out);
  nand nand_27 (nand_27_out, DS_2, DS_2);
  nand nand_28 (nand_28_out, nand_17_out, nand_17_out);
  nand nand_29 (nand_29_out, DS_5, DS_5);
  nand nand_30 (nand_30_out, nand_18_out, nand_18_out);
  nand nand_31 (nand_31_out, DS_8, DS_8);
  nand nand_32 (nand_32_out, DS_9, DS_9);
  nand nand_33 (nand_33_out, nand_19_out, nand_20_out);
  nand nand_34 (nand_34_out, nand_21_out, nand_22_out);
  nand nand_35 (nand_35_out, nand_23_out, nand_24_out);
  nand nand_36 (nand_36_out, nand_25_out, B_1);
  nand nand_37 (nand_37_out, nand_26_out, nand_27_out);
  nand nand_38 (nand_38_out, nand_28_out, nand_29_out);
  nand nand_39 (nand_39_out, nand_30_out, nand_31_out);
  nand nand_40 (nand_40_out, nand_32_out, B_0);
  nand nand_41 (nand_41_out, nand_33_out, nand_33_out);
  nand nand_42 (nand_42_out, nand_34_out, nand_34_out);
  nand nand_43 (nand_43_out, nand_35_out, nand_35_out);
  nand nand_44 (nand_44_out, nand_36_out, nand_36_out);
  nand nand_45 (nand_45_out, nand_37_out, nand_37_out);
  nand nand_46 (nand_46_out, nand_38_out, nand_38_out);
  nand nand_47 (nand_47_out, nand_39_out, nand_39_out);
  nand nand_48 (nand_48_out, nand_40_out, nand_40_out);
  nand nand_49 (nand_49_out, nand_41_out, nand_42_out);
  nand nand_50 (nand_50_out, nand_43_out, nand_44_out);
  nand nand_51 (nand_51_out, nand_45_out, nand_46_out);
  nand nand_52 (nand_52_out, nand_47_out, nand_48_out);
  nand nand_53 (nand_53_out, nand_49_out, nand_49_out);
  nand nand_54 (nand_54_out, nand_50_out, nand_50_out);
  nand nand_55 (nand_55_out, nand_51_out, nand_51_out);
  nand nand_56 (nand_56_out, nand_52_out, nand_52_out);
  nand nand_57 (nand_57_out, nand_53_out, nand_54_out);
  nand nand_58 (nand_58_out, nand_55_out, nand_56_out);
  nand nand_59 (O_1, nand_57_out, nand_57_out);
  nand nand_60 (O_0, nand_58_out, nand_58_out);
endmodule

module transition_logic (
  input  C_3,
  input  C_2,
  input  C_1,
  input  C_0,
  input  B_1,
  input  B_0,
  input  DS_9,
  input  DS_8,
  input  DS_7,
  input  DS_6,
  input  DS_5,
  input  DS_4,
  input  DS_3,
  input  DS_2,
  input  DS_1,
  input  DS_0,
  output S_3,
  output S_2,
  output S_1,
  output S_0,
  output [11:0] input_bus
);

  wire in_impeach_1_o_0, in_impeach_1_o_1;

  in_impeach in_impeach_1 (
    .B_1(B_1), .B_0(B_0), .DS_9(DS_9), .DS_8(DS_8), .DS_7(DS_7), .DS_6(DS_6), .DS_5(DS_5), .DS_4(DS_4),
    .DS_3(DS_3), .DS_2(DS_2), .DS_1(DS_1), .DS_0(DS_0), .O_1(in_impeach_1_o_1), .O_0(in_impeach_1_o_0));
  transition_logic_half transition_logic_half_1 (
    .C_3(C_3), .C_2(C_2), .C_1(C_1), .C_0(C_0), .B_1(in_impeach_1_o_1), .B_0(in_impeach_1_o_0), .S_3(S_3),
    .S_2(S_2), .S_1(S_1), .S_0(S_0));

  assign input_bus = {B_1, B_0, DS_9, DS_8, DS_7, DS_6, DS_5, DS_4, DS_3, DS_2, DS_1, DS_0};
endmodule

module debouncer (
  input  I_0,
  output out_2
);

  wire and_1_out, clock_1_out, d_ff_1_q, d_ff_1_qn, d_ff_2_q;

  Clock clock_1 (.out(clock_1_out));
  D_Flip_Flop d_ff_1 (.D(I_0), .clk(clock_1_out), .Q(d_ff_1_q), .Qn(d_ff_1_qn));  // open: preset, reset
  D_Flip_Flop #(.trigger("falling")) d_ff_2 (
    .D(d_ff_1_qn), .clk(clock_1_out), .Q(d_ff_2_q));  // open: Qn, preset, reset
  D_Flip_Flop #(.trigger("falling")) d_ff_3 (.D(and_1_out), .clk(clock_1_out), .Q(out_2));  // open: Qn, preset, reset
  and and_1 (and_1_out, d_ff_1_q, d_ff_2_q);
endmodule

module reset_mode (
  input  B_1,
  input  B_0,
  output R
);

  wire and_1_out, clock_1_out, d_ff_1_q, d_ff_2_q, d_ff_3_q, d_ff_4_q, t_ff_1_q;

  and and_1 (and_1_out, B_1, B_0);
  Clock clock_1 (.out(clock_1_out));
  T_Flip_Flop t_ff_1 (.T(and_1_out), .clk(clock_1_out), .Q(t_ff_1_q), .reset(d_ff_1_q));  // open: Qn, preset
  D_Flip_Flop d_ff_1 (.D(t_ff_1_q), .clk(clock_1_out), .Q(d_ff_1_q), .reset(d_ff_2_q));  // open: Qn, preset
  D_Flip_Flop d_ff_2 (.D(d_ff_1_q), .clk(clock_1_out), .Q(d_ff_2_q), .reset(d_ff_3_q));  // open: Qn, preset
  D_Flip_Flop d_ff_3 (.D(d_ff_2_q), .clk(clock_1_out), .Q(d_ff_3_q), .reset(d_ff_4_q));  // open: Qn, preset
  D_Flip_Flop d_ff_4 (.D(d_ff_3_q), .clk(clock_1_out), .Q(d_ff_4_q), .reset(d_ff_4_q));  // open: Qn, preset
  and and_2 (R, and_1_out, d_ff_3_q);
endmodule

module binary_to_time_converter (
  input  [4:0] in_1,
  input  [4:0] in_2,
  output [5:0] out_3
);

  wire nand_1_out, nand_2_out, nand_3_out, nand_4_out, nand_5_out, nand_6_out, nand_7_out, nand_8_out,
       nand_9_out, nand_10_out, nand_11_out, nand_12_out, nand_13_out, nand_14_out, nand_15_out, nand_16_out,
       nand_17_out, nand_18_out, nand_19_out, nand_20_out, nand_21_out, nand_22_out, nand_23_out,
       nand_24_out, nand_25_out, nand_26_out, nand_27_out, nand_28_out, nand_29_out, nand_30_out,
       nand_31_out, nand_32_out, nand_33_out, nand_34_out, nand_35_out, nand_36_out, nand_37_out,
       nand_38_out, nand_39_out, nand_40_out, nand_41_out, nand_42_out, nand_43_out, nand_44_out,
       nand_45_out, nand_46_out, nand_47_out, nand_48_out, nand_49_out, nand_50_out, nand_51_out,
       nand_52_out, nand_53_out, nand_54_out, nand_55_out, nand_56_out, nand_57_out, nand_58_out,
       nand_59_out, nand_60_out, nand_61_out, nand_62_out, nand_63_out, nand_64_out, nand_65_out,
       nand_66_out, nand_67_out, nand_68_out, nand_69_out, nand_71_out, nand_72_out, nand_73_out,
       nand_74_out, nand_75_out, nand_76_out, nand_77_out, nand_78_out, nand_79_out, nand_80_out,
       nand_81_out, nand_82_out, nand_83_out, nand_84_out, nand_85_out, nand_86_out, nand_87_out,
       nand_88_out, nand_89_out, nand_90_out, nand_91_out, nand_92_out, nand_93_out, nand_94_out,
       nand_95_out, nand_96_out, nand_97_out, nand_98_out, nand_99_out, nand_100_out, nand_101_out,
       nand_102_out, nand_103_out, nand_104_out, nand_105_out, nand_106_out, nand_107_out, nand_108_out,
       nand_109_out, nand_110_out, nand_111_out, nand_112_out, nand_113_out, nand_114_out, nand_115_out,
       nand_116_out, nand_117_out, nand_118_out, nand_119_out, nand_120_out, nand_121_out, nand_122_out,
       nand_123_out, nand_124_out, nand_126_out, nand_127_out, nand_128_out, nand_129_out, nand_130_out,
       nand_131_out, nand_132_out, nand_133_out, nand_134_out, nand_135_out, nand_136_out, nand_137_out,
       nand_138_out, nand_139_out, nand_140_out, nand_141_out, nand_142_out, nand_143_out, nand_144_out,
       nand_145_out, nand_146_out, nand_147_out, nand_148_out, nand_149_out, nand_150_out, nand_151_out,
       nand_152_out, nand_153_out, nand_154_out, nand_155_out, nand_156_out, nand_157_out, nand_158_out,
       nand_159_out, nand_160_out, nand_161_out, nand_162_out, nand_163_out, nand_164_out, nand_165_out,
       nand_168_out, nand_169_out, nand_171_out, nand_172_out;

  nand nand_1 (nand_1_out, in_2[2], in_2[2]);
  nand nand_2 (nand_2_out, in_2[0], in_2[0]);
  nand nand_3 (nand_3_out, in_1[1], in_1[1]);
  nand nand_4 (nand_4_out, in_1[1], in_1[1]);
  nand nand_5 (nand_5_out, in_2[3], in_2[3]);
  nand nand_6 (nand_6_out, in_2[2], in_2[2]);
  nand nand_7 (nand_7_out, in_2[1], in_2[1]);
  nand nand_8 (nand_8_out, in_1[2], in_1[2]);
  nand nand_9 (nand_9_out, in_1[1], in_1[1]);
  nand nand_10 (nand_10_out, in_1[2], in_1[2]);
  nand nand_11 (nand_11_out, in_1[1], in_1[1]);
  nand nand_12 (nand_12_out, in_1[2], in_1[2]);
  nand nand_13 (nand_13_out, in_1[1], in_1[1]);
  nand nand_14 (nand_14_out, in_1[0], in_1[0]);
  nand nand_15 (nand_15_out, in_1[1], in_1[1]);
  nand nand_16 (nand_16_out, in_1[0], in_1[0]);
  nand nand_17 (nand_17_out, in_2[2], in_2[2]);
  nand nand_18 (nand_18_out, in_1[0], in_1[0]);
  nand nand_19 (nand_19_out, in_2[1], in_2[1]);
  nand nand_20 (nand_20_out, in_2[2], in_2[2]);
  nand nand_21 (nand_21_out, in_2[3], nand_1_out);
  nand nand_22 (nand_22_out, in_2[1], nand_2_out);
  nand nand_23 (nand_23_out, in_1[1], in_1[0]);
  nand nand_24 (nand_24_out, nand_3_out, in_1[0]);
  nand nand_25 (nand_25_out, in_2[2], in_2[1]);
  nand nand_26 (nand_26_out, nand_4_out, in_1[0]);
  nand nand_27 (nand_27_out, in_1[1], nand_5_out);
  nand nand_28 (nand_28_out, nand_6_out, nand_7_out);
  nand nand_29 (nand_29_out, nand_8_out, nand_9_out);
  nand nand_30 (nand_30_out, nand_10_out, nand_11_out);
  nand nand_31 (nand_31_out, nand_12_out, in_1[0]);
  nand nand_32 (nand_32_out, nand_13_out, nand_14_out);
  nand nand_33 (nand_33_out, nand_15_out, in_2[2]);
  nand nand_34 (nand_34_out, in_1[1], nand_16_out);
  nand nand_35 (nand_35_out, in_1[1], nand_17_out);
  nand nand_36 (nand_36_out, nand_18_out, in_2[1]);
  nand nand_37 (nand_37_out, in_1[0], nand_19_out);
  nand nand_38 (nand_38_out, in_2[3], nand_20_out);
  nand nand_39 (nand_39_out, nand_21_out, nand_21_out);
  nand nand_40 (nand_40_out, nand_22_out, nand_22_out);
  nand nand_41 (nand_41_out, nand_23_out, nand_23_out);
  nand nand_42 (nand_42_out, nand_24_out, nand_24_out);
  nand nand_43 (nand_43_out, nand_25_out, nand_25_out);
  nand nand_44 (nand_44_out, nand_26_out, nand_26_out);
  nand nand_45 (nand_45_out, nand_27_out, nand_27_out);
  nand nand_46 (nand_46_out, nand_28_out, nand_28_out);
  nand nand_47 (nand_47_out, in_1[2], in_1[2]);
  nand nand_48 (nand_48_out, in_1[0], in_1[0]);
  nand nand_49 (nand_49_out, nand_29_out, nand_29_out);
  nand nand_50 (nand_50_out, in_2[3], in_2[3]);
  nand nand_51 (nand_51_out, in_2[2], in_2[2]);
  nand nand_52 (nand_52_out, nand_30_out, nand_30_out);
  nand nand_53 (nand_53_out, in_2[3], in_2[3]);
  nand nand_54 (nand_54_out, in_2[1], in_2[1]);
  nand nand_55 (nand_55_out, nand_31_out, nand_31_out);
  nand nand_56 (nand_56_out, in_2[3], in_2[3]);
  nand nand_57 (nand_57_out, in_2[2], in_2[2]);
  nand nand_58 (nand_58_out, in_2[1], in_2[1]);
  nand nand_59 (nand_59_out, in_1[0], in_1[0]);
  nand nand_60 (nand_60_out, in_1[0], in_1[0]);
  nand nand_61 (nand_61_out, nand_32_out, nand_32_out);
  nand nand_62 (nand_62_out, nand_33_out, nand_33_out);
  nand nand_63 (nand_63_out, in_2[1], in_2[1]);
  nand nand_64 (nand_64_out, in_1[1], in_1[1]);
  nand nand_65 (nand_65_out, in_2[2], in_2[2]);
  nand nand_66 (nand_66_out, nand_34_out, nand_34_out);
  nand nand_67 (nand_67_out, in_2[2], in_2[2]);
  nand nand_68 (nand_68_out, nand_35_out, nand_35_out);
  nand nand_69 (nand_69_out, in_2[1], in_2[1]);
  nand nand_70 (out_3[1], nand_36_out, nand_37_out);
  nand nand_71 (nand_71_out, nand_38_out, nand_38_out);
  nand nand_72 (nand_72_out, nand_39_out, nand_40_out);
  nand nand_73 (nand_73_out, nand_41_out, in_2[1]);
  nand nand_74 (nand_74_out, in_1[1], in_1[0]);
  nand nand_75 (nand_75_out, in_1[1], in_1[0]);
  nand nand_76 (nand_76_out, nand_42_out, nand_43_out);
  nand nand_77 (nand_77_out, nand_44_out, in_2[3]);
  nand nand_78 (nand_78_out, nand_45_out, nand_46_out);
  nand nand_79 (nand_79_out, in_1[2], in_2[3]);
  nand nand_80 (nand_80_out, nand_47_out, nand_48_out);
  nand nand_81 (nand_81_out, nand_49_out, in_1[0]);
  nand nand_82 (nand_82_out, nand_50_out, nand_51_out);
  nand nand_83 (nand_83_out, nand_52_out, in_1[0]);
  nand nand_84 (nand_84_out, nand_53_out, nand_54_out);
  nand nand_85 (nand_85_out, nand_55_out, nand_56_out);
  nand nand_86 (nand_86_out, nand_57_out, nand_58_out);
  nand nand_87 (nand_87_out, in_1[1], nand_59_out);
  nand nand_88 (nand_88_out, in_1[2], nand_60_out);
  nand nand_89 (nand_89_out, in_1[2], in_2[2]);
  nand nand_90 (nand_90_out, in_1[2], in_1[0]);
  nand nand_91 (nand_91_out, nand_61_out, in_2[2]);
  nand nand_92 (nand_92_out, nand_62_out, nand_63_out);
  nand nand_93 (nand_93_out, nand_64_out, in_1[0]);
  nand nand_94 (nand_94_out, nand_65_out, in_2[1]);
  nand nand_95 (nand_95_out, nand_66_out, nand_67_out);
  nand nand_96 (nand_96_out, nand_68_out, nand_69_out);
  nand nand_97 (nand_97_out, in_1[1], in_1[0]);
  nand nand_98 (nand_98_out, in_2[2], in_2[1]);
  nand nand_99 (nand_99_out, in_2[0], in_2[0]);
  nand nand_100 (nand_100_out, nand_71_out, in_2[1]);
  nand nand_101 (nand_101_out, nand_72_out, nand_73_out);
  nand nand_102 (nand_102_out, nand_74_out, nand_74_out);
  nand nand_103 (nand_103_out, nand_75_out, nand_75_out);
  nand nand_104 (nand_104_out, nand_76_out, nand_77_out);
  nand nand_105 (nand_105_out, in_1[0], in_1[0]);
  nand nand_106 (nand_106_out, nand_78_out, nand_79_out);
  nand nand_107 (nand_107_out, nand_80_out, nand_80_out);
  nand nand_108 (nand_108_out, nand_81_out, nand_81_out);
  nand nand_109 (nand_109_out, nand_82_out, nand_82_out);
  nand nand_110 (nand_110_out, nand_83_out, nand_83_out);
  nand nand_111 (nand_111_out, nand_84_out, nand_84_out);
  nand nand_112 (nand_112_out, nand_85_out, nand_85_out);
  nand nand_113 (nand_113_out, nand_86_out, nand_86_out);
  nand nand_114 (nand_114_out, nand_87_out, nand_87_out);
  nand nand_115 (nand_115_out, nand_88_out, nand_88_out);
  nand nand_116 (nand_116_out, in_2[3], in_2[3]);
  nand nand_117 (nand_117_out, nand_89_out, nand_89_out);
  nand nand_118 (nand_118_out, nand_90_out, nand_90_out);
  nand nand_119 (nand_119_out, nand_91_out, nand_92_out);
  nand nand_120 (nand_120_out, nand_93_out, nand_93_out);
  nand nand_121 (nand_121_out, nand_94_out, nand_94_out);
  nand nand_122 (nand_122_out, nand_95_out, nand_96_out);
  nand nand_123 (nand_123_out, nand_97_out, nand_97_out);
  nand nand_124 (nand_124_out, nand_98_out, nand_98_out);
  nand nand_125 (out_3[0], nand_99_out, nand_100_out);
  nand nand_126 (nand_126_out, nand_101_out, nand_101_out);
  nand nand_127 (nand_127_out, nand_102_out, in_2[2]);
  nand nand_128 (nand_128_out, nand_103_out, in_2[3]);
  nand nand_129 (nand_129_out, in_1[2], in_1[2]);
  nand nand_130 (nand_130_out, nand_104_out, nand_104_out);
  nand nand_131 (nand_131_out, in_1[1], nand_105_out);
  nand nand_132 (nand_132_out, nand_106_out, nand_106_out);
  nand nand_133 (nand_133_out, in_1[2], in_1[0]);
  nand nand_134 (nand_134_out, nand_107_out, in_2[3]);
  nand nand_135 (nand_135_out, nand_108_out, nand_109_out);
  nand nand_136 (nand_136_out, nand_110_out, nand_111_out);
  nand nand_137 (nand_137_out, nand_112_out, nand_113_out);
  nand nand_138 (nand_138_out, nand_114_out, in_2[2]);
  nand nand_139 (nand_139_out, nand_115_out, nand_116_out);
  nand nand_140 (nand_140_out, nand_117_out, in_2[1]);
  nand nand_141 (nand_141_out, nand_118_out, in_2[3]);
  nand nand_142 (nand_142_out, nand_119_out, nand_119_out);
  nand nand_143 (nand_143_out, nand_120_out, nand_121_out);
  nand nand_144 (nand_144_out, nand_122_out, nand_122_out);
  nand nand_145 (nand_145_out, nand_123_out, nand_124_out);
  nand nand_146 (nand_146_out, nand_126_out, nand_127_out);
  nand nand_147 (nand_147_out, nand_128_out, nand_129_out);
  nand nand_148 (nand_148_out, nand_130_out, nand_131_out);
  nand nand_149 (nand_149_out, nand_132_out, nand_133_out);
  nand nand_150 (nand_150_out, nand_134_out, nand_135_out);
  nand nand_151 (nand_151_out, nand_136_out, nand_137_out);
  nand nand_152 (nand_152_out, nand_138_out, nand_139_out);
  nand nand_153 (nand_153_out, nand_140_out, nand_141_out);
  nand nand_154 (nand_154_out, nand_142_out, nand_143_out);
  nand nand_155 (nand_155_out, nand_144_out, nand_145_out);
  nand nand_156 (nand_156_out, nand_146_out, nand_146_out);
  nand nand_157 (nand_157_out, nand_147_out, nand_147_out);
  nand nand_158 (nand_158_out, nand_148_out, nand_148_out);
  nand nand_159 (nand_159_out, nand_149_out, nand_149_out);
  nand nand_160 (nand_160_out, nand_150_out, nand_150_out);
  nand nand_161 (nand_161_out, nand_151_out, nand_151_out);
  nand nand_162 (nand_162_out, nand_152_out, nand_152_out);
  nand nand_163 (nand_163_out, nand_153_out, nand_153_out);
  nand nand_164 (nand_164_out, nand_154_out, nand_154_out);
  nand nand_165 (nand_165_out, nand_155_out, nand_155_out);
  nand nand_166 (out_3[5], nand_156_out, nand_157_out);
  nand nand_167 (out_3[4], nand_158_out, nand_159_out);
  nand nand_168 (nand_168_out, nand_160_out, nand_161_out);
  nand nand_169 (nand_169_out, nand_162_out, nand_163_out);
  nand nand_170 (out_3[2], nand_164_out, nand_165_out);
  nand nand_171 (nand_171_out, nand_168_out, nand_168_out);
  nand nand_172 (nand_172_out, nand_169_out, nand_169_out);
  nand nand_173 (out_3[3], nand_171_out, nand_172_out);
endmodule
